// Logisim project A2024_5a.circ as structural Verilog
module main (
  input  [31:0] in_1,
  input  in_2,
  input  [1:0] in_3,
  input  in_4,
  input  in_5
);

  wire Ack_ID, Ack_ILDF, AckCFU, AckInjector, AckPC, ALU_A_In, ALU_B_In, ALU_C_Out, Check_CB_In, CheckBool,
       CheckCall, CodeBlock_IN, Else_Change, Elseif_Change, If_Change, LSU_Add_Offset, LSU_Pick,
       LSU_Reset_Offset, LSU_Sub_Offset, LU_A_In, LU_B_In, LU_F_In, Pass_Data1, Pass_Immediate, Read_Memory,
       Read_Scratchpad, ReqPC, ReqPop, Start_out, Write_Memory, Write_Scratchpad;
  wire [1:0] Call, injector_1_call_or_push_out;
  wire [2:0] LU_F;
  wire [3:0] ALU_F;
  wire [7:0] Byte_1_data, Byte_2_data, Byte_3_data, Byte_4_data, controlled_buffer_1_out,
       instruction_decoder_1_op1, instruction_decoder_1_op2, pull_resistor_3_node, pull_resistor_4_node,
       stack_1_items;
  wire [15:0] programcounter_1_ram1, programcounter_1_ram2, programcounter_1_ram3, programcounter_1_ram4,
       rom_1_data, rom_2_data, stack_1_codeblockid;
  wire [31:0] CodeBlock, injector_1_codeblock_out;
  wire [47:0] instlengthdecfast_1_instruction;

  Button Start (.out(Start_out));
  Injector injector_1 (
    .Beginn(Start_out), .Start_CodeBlock({16{1'b0}}), .CodeBlock_IN(in_1), .Call_or_Push(in_3), .Stop(in_4),
    .Acknowledge(AckInjector), .CodeBlock_OUT(injector_1_codeblock_out),
    .Call_or_Push_OUT(injector_1_call_or_push_out), .AckPrev(AckCFU));
  // Probe on stack_1_items
  Stack stack_1 (
    .Push_Data(injector_1_codeblock_out), .Call_oder_Push(injector_1_call_or_push_out), .PushStop(in_2),
    .ReqPost(ReqPop), .Items(stack_1_items), .CodeBlockID(stack_1_codeblockid), .AckPost(AckPC),
    .AckPrev(AckInjector));
  // Probe on stack_1_codeblockid
  ROM #(.addrWidth(16), .dataWidth(16)) rom_1 (.addr(stack_1_codeblockid), .data(rom_1_data));
  ROM #(.addrWidth(16), .dataWidth(16)) rom_2 (.addr(stack_1_codeblockid), .data(rom_2_data));
  ProgramCounter programcounter_1 (
    .Start(rom_1_data), .Steps(rom_2_data), .AckPrev(AckPC), .ReqPost(ReqPC), .Stop(in_5),
    .RAM1(programcounter_1_ram1), .RAM2(programcounter_1_ram2), .RAM3(programcounter_1_ram3),
    .RAM4(programcounter_1_ram4), .ReqPrev(ReqPop), .AckPost(Ack_ILDF));  // open: ActiveRAMs
  // Probe on programcounter_1_ram1
  ROM #(.addrWidth(16)) Byte_1 (.addr(programcounter_1_ram1), .data(Byte_1_data));
  ROM #(.addrWidth(16)) Byte_2 (.addr(programcounter_1_ram2), .data(Byte_2_data));
  ROM #(.addrWidth(16)) Byte_3 (.addr(programcounter_1_ram3), .data(Byte_3_data));
  ROM #(.addrWidth(16)) Byte_4 (.addr(programcounter_1_ram4), .data(Byte_4_data));
  InstLengthDecFast instlengthdecfast_1 (
    .Byte_1(Byte_1_data), .Byte_2(Byte_2_data), .Byte_3(Byte_3_data), .Byte_4(Byte_4_data),
    .PrevAck(Ack_ILDF), .PostAck(Ack_ID), .Instruction(instlengthdecfast_1_instruction), .ReqPrev(ReqPC));
  Instruction_Decoder instruction_decoder_1 (
    .Instruction(instlengthdecfast_1_instruction), .OP1(instruction_decoder_1_op1),
    .OP2(instruction_decoder_1_op2), .If_Change(If_Change), .Elseif_Change(Elseif_Change),
    .Else_Change(Else_Change), .LU_F(LU_F), .LU_F_In(LU_F_In), .LU_A_In(LU_A_In), .LU_B_In(LU_B_In),
    .LSU_Pick(LSU_Pick), .LSU_Add_Offset(LSU_Add_Offset), .LSU_Sub_Offset(LSU_Sub_Offset),
    .LSU_Reset_Offset(LSU_Reset_Offset), .WriteMemory(Write_Memory), .ReadMemory(Read_Memory), .ALU_F(ALU_F),
    .ALU_A_In(ALU_A_In), .ALU_B_In(ALU_B_In), .ALU_C_Out(ALU_C_Out), .Call(CheckCall),
    .CodeBlock_IN(Check_CB_In), .Pass_Immediate(Pass_Immediate), .CheckBool(CheckBool),
    .Pass_Data1(Pass_Data1), .Read_Scratchpad(Read_Scratchpad), .Write_Scratchpad(Write_Scratchpad),
    .AckPrev(Ack_ID));  // open: Signals_Out
  Pull_Resistor pull_resistor_1 (.node(instruction_decoder_1_op1));
  Pull_Resistor pull_resistor_2 (.node(instruction_decoder_1_op2));
  Pull_Resistor pull_resistor_3 (.node(pull_resistor_3_node));
  Pull_Resistor pull_resistor_4 (.node(pull_resistor_4_node));
  assign controlled_buffer_1_out = Pass_Data1 ? pull_resistor_3_node : 8'bz;  // Controlled_Buffer controlled_buffer_1
  assign controlled_buffer_1_out = Pass_Immediate ? instruction_decoder_1_op1 : 8'bz;  // Controlled_Buffer controlled_buffer_2
  LSU lsu_1 (
    .AddrNr(instruction_decoder_1_op1), .DeltaOffset(pull_resistor_3_node), .Data_In(pull_resistor_3_node),
    .Pick(LSU_Pick), .Add_Offset(LSU_Add_Offset), .Sub_Offset(LSU_Sub_Offset),
    .ResetOffset(LSU_Reset_Offset), .Write(Write_Memory), .Read(Read_Memory),
    .Bus_Out(controlled_buffer_1_out));  // open: CLK
  ALU alu_1 (
    .Funktion(ALU_F), .A(pull_resistor_3_node), .A_In(ALU_A_In), .B(pull_resistor_4_node), .B_In(ALU_B_In),
    .C_Out(ALU_C_Out), .C(controlled_buffer_1_out));  // open: CLK
  ControlFlow_Unit controlflow_unit_1 (
    .Funktion(LU_F), .LU_F_In(LU_F_In), .A(pull_resistor_3_node), .LU_A_In(LU_A_In),
    .B(pull_resistor_4_node), .LU_B_In(LU_B_In), .If_Change_Bool(If_Change),
    .Elseif_Change_Bool(Elseif_Change), .Else_Change_Bool(Else_Change), .Operand1(instruction_decoder_1_op1),
    .Operand2(instruction_decoder_1_op2), .CheckCall(CheckCall), .Check_CB_In(Check_CB_In),
    .CheckBool(CheckBool), .Codeblock(CodeBlock), .Call(Call), .CodeBlock_In(CodeBlock_IN));  // open: CLK
  Scratchpad scratchpad_1 (
    .Data_In(pull_resistor_4_node), .Addr(instruction_decoder_1_op1), .Write(Write_Scratchpad),
    .Read(Read_Scratchpad), .Data_Out(controlled_buffer_1_out));  // open: CLK
  Pull_Resistor pull_resistor_5 (.node(controlled_buffer_1_out));
  Belt belt_1 ();  // open: R1, R2, Data_In, Write_Belt, CLK, R1_Data, R2_Data

  // Notes on the sheet:
  //   contents of rom_1 (hex, n*v repeats v):
  //   0 12 126*0 800 600
  //   contents of rom_2 (hex, n*v repeats v):
  //   3 1f 126*0 2 20
  //   CodeBlock Table
  //   Start
  //   Schritte
  //   Wenn der Block in 0x0000-0x7fff gespeichert ist, beinhaltet er einen Call
  //   Wenn der Block in 0x8000-0xffff gespeichert ist, beinhaltet er keinen Call
  //   Achtung: Operand forward ist noch nicht implementiert!!! Voneinander abhängige Instructions direkt nacheinander funktionieren nicht!!!
  //   contents of Byte_1 (hex, n*v repeats v):
  //   82 41 50 53 15*0 6 0 7 f e0 e1 0 2 0 1 10 e0 e1 11 e3 e3 12 e3 e4 c e5 3 2 80 1 81 37*0 ff ff d e 1
  //   937*0 5 ef 9 4 80 3 81 505*0 f 12 0 4 10 e0 e e0 d 15 1 14 1 2
  //   contents of Byte_2 (hex, n*v repeats v):
  //   0 aa 1 77*0 12 34 0 0 a a 0 0 2
  //   contents of Byte_3 (hex, n*v repeats v):
  //   0 48 80 81*0 1
  //   contents of Byte_4 (hex, n*v repeats v):
  //   11 0 12 81*0 1
  //   Programmspeicher
  //   Belt kann parallel zu decoden der Opcodes ausgelesen werden.
endmodule

module Stack (
  input  [31:0] Push_Data,
  input  [1:0] Call_oder_Push,
  input  PushStop,
  input  ReqPost,
  output [7:0] Items,
  output [15:0] CodeBlockID,
  output AckPost,
  output AckPrev
);

  wire and_1_out, and_2_out, and_4_out, and_5_out, and_6_out, buffer_1_out, buffer_2_out, buffer_3_out,
       buffer_4_out, buffer_5_out, buffer_6_out, buffer_7_out, buffer_8_out, buffer_9_out, buffer_10_out,
       buffer_11_out, buffer_12_out, buffer_13_out, buffer_14_out, buffer_15_out, buffer_16_out,
       buffer_17_out, buffer_18_out, buffer_19_out, buffer_20_out, buffer_21_out, buffer_22_out,
       buffer_23_out, buffer_24_out, buffer_25_out, buffer_26_out, buffer_27_out, buffer_28_out,
       buffer_29_out, buffer_30_out, buffer_31_out, buffer_32_out, buffer_33_out, buffer_34_out,
       buffer_35_out, buffer_36_out, buffer_37_out, buffer_38_out, buffer_39_out, buffer_40_out,
       buffer_41_out, buffer_42_out, buffer_43_out, buffer_44_out, Call, Decrement,
       drailbitreceiverfull_1_allchanged, drailbitreceiverfull_1_bit, drailbytereceiver_1_allchanged,
       drailbytereceiver_2_delaystart, edgedetector_1_out_2, edgedetector_2_out_2, edgedetector_3_out_2,
       Increment, LastPush, mit_Call, not_1_out, not_2_out, not_3_out, not_4_out, not_5_out, not_6_out,
       not_7_out, or_1_out, or_2_out, Pop_Stop, posedgedetector_1_out_2, posedgedetector_2_out_2, Push_Stop,
       s_r_ff_1_q, s_r_ff_2_q, s_r_ff_3_q, s_r_ff_4_qn, s_r_ff_5_q, s_r_ff_6_q, s_r_ff_7_qn, s_r_ff_8_q,
       t_ff_1_q;
  wire [7:0] adder_1_out, drailbytereceiver_1_byte, drailbytereceiver_2_byte, multiplexer_1_out,
       pull_resistor_1_node, subtractor_1_out, subtractor_2_out;
  wire [15:0] ram_1_dout;

  T_Flip_Flop t_ff_1 (.T(1'b1), .clk(Increment), .Q(t_ff_1_q));  // open: Qn, reset, preset
  buf buffer_1 (buffer_1_out, Items[0]);
  buf buffer_2 (buffer_2_out, buffer_1_out);
  buf buffer_3 (buffer_3_out, buffer_2_out);
  buf buffer_4 (buffer_4_out, buffer_3_out);
  buf buffer_5 (buffer_5_out, buffer_4_out);
  DRailBitReceiverFull drailbitreceiverfull_1 (
    .Stop(PushStop), .ReadyDelay(t_ff_1_q), .DualRailBit(Call_oder_Push), .OtherBytesChanged(1'b1),
    .AllChanged(drailbitreceiverfull_1_allchanged), .Bit(drailbitreceiverfull_1_bit));  // open: DelayStart, Acknowledge
  DRailByteReceiver drailbytereceiver_1 (
    .Stop(PushStop), .ReadyDelay(t_ff_1_q), .DualRailByte(Push_Data[15:0]),
    .OtherBytesChanged(drailbitreceiverfull_1_allchanged), .AllChanged(drailbytereceiver_1_allchanged),
    .Byte(drailbytereceiver_1_byte));  // open: DelayStart, Acknowledge
  DRailByteReceiver drailbytereceiver_2 (
    .Stop(PushStop), .ReadyDelay(t_ff_1_q), .DualRailByte(Push_Data[31:16]),
    .OtherBytesChanged(drailbytereceiver_1_allchanged), .DelayStart(drailbytereceiver_2_delaystart),
    .Acknowledge(AckPrev), .Byte(drailbytereceiver_2_byte));  // open: AllChanged
  buf buffer_6 (buffer_6_out, buffer_5_out);
  buf buffer_7 (buffer_7_out, buffer_6_out);
  buf buffer_8 (buffer_8_out, buffer_7_out);
  PosEdgeDetector posedgedetector_1 (.in_1(Increment), .out_2(posedgedetector_1_out_2));
  S_R_Flip_Flop s_r_ff_1 (.Q(s_r_ff_1_q), .reset(and_1_out), .preset(posedgedetector_1_out_2));  // open: S, R, clk, Qn
  PosEdgeDetector posedgedetector_2 (.in_1(Decrement), .out_2(posedgedetector_2_out_2));
  S_R_Flip_Flop s_r_ff_2 (.Q(s_r_ff_2_q), .reset(and_2_out), .preset(posedgedetector_2_out_2));  // open: S, R, clk, Qn
  EdgeDetector edgedetector_1 (.in_1(buffer_8_out), .out_2(edgedetector_1_out_2));
  EdgeDetector edgedetector_2 (.in_1(drailbytereceiver_2_delaystart), .out_2(edgedetector_2_out_2));
  not not_1 (not_1_out, Push_Stop);
  not not_2 (not_2_out, Pop_Stop);
  buf buffer_9 (buffer_9_out, or_1_out);
  buf buffer_10 (buffer_10_out, edgedetector_1_out_2);
  buf buffer_11 (buffer_11_out, buffer_10_out);
  buf buffer_12 (buffer_12_out, buffer_11_out);
  not not_3 (not_3_out, Push_Stop);
  S_R_Flip_Flop s_r_ff_3 (.Q(s_r_ff_3_q), .reset(Increment), .preset(edgedetector_2_out_2));  // open: S, R, clk, Qn
  and and_1 (and_1_out, not_1_out, s_r_ff_1_q);
  S_R_Flip_Flop s_r_ff_4 (.Q(LastPush), .reset(and_2_out), .Qn(s_r_ff_4_qn), .preset(and_1_out));  // open: S, R, clk
  and and_2 (and_2_out, not_2_out, s_r_ff_2_q);
  Adder adder_1 (.a(Items), .b(8'h1), .out(adder_1_out));  // open: cin, cout
  Subtractor subtractor_1 (.a(Items), .b(8'h1), .out(subtractor_1_out));  // open: bin, bout
  buf buffer_13 (buffer_13_out, buffer_15_out);
  buf buffer_14 (buffer_14_out, buffer_13_out);
  buf buffer_15 (buffer_15_out, buffer_9_out);
  buf buffer_16 (buffer_16_out, buffer_18_out);
  buf buffer_17 (buffer_17_out, buffer_16_out);
  buf buffer_18 (buffer_18_out, buffer_12_out);
  D_Flip_Flop d_ff_1 (.D(drailbitreceiverfull_1_bit), .clk(and_5_out), .Q(Call));  // open: Qn, preset, reset
  and and_3 (Increment, not_3_out, s_r_ff_3_q);
  or or_1 (or_1_out, and_1_out, and_2_out);
  buf buffer_19 (buffer_19_out, buffer_14_out);
  buf buffer_20 (buffer_20_out, buffer_19_out);
  not not_4 (not_4_out, LastPush);
  buf buffer_21 (buffer_21_out, buffer_17_out);
  buf buffer_22 (buffer_22_out, buffer_21_out);
  // Probe on {drailbytereceiver_2_byte, drailbytereceiver_1_byte}
  S_R_Flip_Flop s_r_ff_5 (.Q(s_r_ff_5_q), .reset(or_2_out), .preset(Increment));  // open: S, R, clk, Qn
  or or_2 (or_2_out, and_5_out, and_4_out);
  Register register_1 (.D(multiplexer_1_out), .en(1'b1), .clk(buffer_24_out), .Q(Items));  // open: clr
  Multiplexer #(.width(8)) multiplexer_1 (
    .in0(adder_1_out), .in1(subtractor_1_out), .out(multiplexer_1_out), .sel(s_r_ff_4_qn));
  buf buffer_23 (buffer_23_out, buffer_20_out);
  buf buffer_24 (buffer_24_out, buffer_23_out);
  and and_4 (and_4_out, not_4_out, buffer_22_out);
  and and_5 (and_5_out, LastPush, buffer_22_out);
  RAM #(.dataWidth(16)) ram_1 (
    .addr(pull_resistor_1_node), .we(s_r_ff_5_q), .oe(1'b1), .clk(or_2_out),
    .din({drailbytereceiver_2_byte, drailbytereceiver_1_byte}), .dout(ram_1_dout));
  S_R_Flip_Flop s_r_ff_6 (.Q(s_r_ff_6_q), .reset(buffer_24_out), .preset(and_5_out));  // open: S, R, clk, Qn
  buf buffer_25 (buffer_25_out, and_4_out);
  buf buffer_26 (buffer_26_out, buffer_25_out);
  buf buffer_27 (buffer_27_out, buffer_26_out);
  buf buffer_28 (buffer_28_out, buffer_27_out);
  buf buffer_29 (buffer_29_out, buffer_28_out);
  and and_6 (and_6_out, Call, s_r_ff_6_q);
  Comparator #(.mode("unsigned")) comparator_1 (.a(Items), .b({8{1'b0}}), .eq(Pop_Stop));  // open: gt, lt
  Comparator #(.mode("unsigned")) comparator_2 (.a(Items), .b({8{1'b1}}), .eq(Push_Stop));  // open: gt, lt
  Pull_Resistor pull_resistor_1 (.node(pull_resistor_1_node));
  not not_5 (not_5_out, Pop_Stop);
  assign pull_resistor_1_node = not_5_out ? subtractor_2_out : 8'bz;  // Controlled_Buffer controlled_buffer_1
  Subtractor subtractor_2 (.a(Items), .b(8'h1), .out(subtractor_2_out));  // open: bin, bout
  buf buffer_30 (buffer_30_out, buffer_29_out);
  buf buffer_31 (buffer_31_out, buffer_30_out);
  S_R_Flip_Flop s_r_ff_7 (.reset(and_6_out), .Qn(s_r_ff_7_qn), .preset(mit_Call));  // open: S, R, clk, Q
  EdgeDetector edgedetector_3 (.in_1(ReqPost), .out_2(edgedetector_3_out_2));
  buf buffer_32 (buffer_32_out, buffer_31_out);
  Pull_Resistor pull_resistor_2 (.node(ram_1_dout));
  // Probe on ram_1_dout
  not not_6 (not_6_out, Pop_Stop);
  S_R_Flip_Flop s_r_ff_8 (.Q(s_r_ff_8_q), .reset(Decrement), .preset(edgedetector_3_out_2));  // open: S, R, clk, Qn
  and and_7 (Decrement, not_6_out, s_r_ff_7_qn, s_r_ff_8_q);
  Register #(.width(16)) register_2 (.D(ram_1_dout), .en(1'b1), .clk(buffer_32_out), .Q(CodeBlockID));  // open: clr
  not not_7 (not_7_out, ram_1_dout[15]);
  and and_8 (mit_Call, not_7_out, buffer_32_out);
  buf buffer_33 (buffer_33_out, buffer_32_out);
  buf buffer_34 (buffer_34_out, buffer_33_out);
  buf buffer_35 (buffer_35_out, buffer_34_out);
  buf buffer_36 (buffer_36_out, buffer_35_out);
  buf buffer_37 (buffer_37_out, buffer_36_out);
  buf buffer_38 (buffer_38_out, buffer_37_out);
  buf buffer_39 (buffer_39_out, buffer_38_out);
  buf buffer_40 (buffer_40_out, buffer_39_out);
  buf buffer_41 (buffer_41_out, buffer_40_out);
  buf buffer_42 (buffer_42_out, buffer_41_out);
  buf buffer_43 (buffer_43_out, buffer_42_out);
  T_Flip_Flop t_ff_2 (.T(1'b1), .clk(buffer_44_out), .Q(AckPost));  // open: Qn, reset, preset
  buf buffer_44 (buffer_44_out, buffer_43_out);

  // Notes on the sheet:
  //   darf nicht bei pull unter 0
  //   push und pop erst mal keine direkte übergabe
  //   Pop Sperre
  //   call im codeblock wird mit der addresse im CodeBlock Memory beschrieben
endmodule

module ProgramCounter (
  input  [15:0] Start,
  input  [15:0] Steps,
  input  AckPrev,
  input  ReqPost,
  input  Stop,
  output [15:0] RAM1,
  output [15:0] RAM2,
  output [15:0] RAM3,
  output [15:0] RAM4,
  output [3:0] ActiveRAMs,
  output ReqPrev,
  output AckPost
);

  wire and_1_out, and_2_out, buffer_1_out, buffer_2_out, buffer_3_out, buffer_4_out, buffer_5_out,
       buffer_6_out, buffer_7_out, buffer_8_out, buffer_9_out, buffer_10_out, buffer_11_out, buffer_12_out,
       buffer_13_out, buffer_14_out, buffer_15_out, buffer_16_out, buffer_17_out, buffer_18_out,
       buffer_19_out, buffer_20_out, buffer_21_out, buffer_22_out, buffer_23_out, buffer_25_out,
       buffer_26_out, buffer_27_out, buffer_28_out, buffer_29_out, buffer_30_out, buffer_31_out,
       comparator_1_eq, Count, edgedetector_1_out_2, edgedetector_2_out_2, not_1_out, not_2_out, not_3_out,
       PC_Fertig, posedgedetector_1_out_2, s_r_ff_1_q, s_r_ff_2_q, t_ff_1_q;
  wire [15:0] adder_1_out, adder_2_out, adder_3_out, adder_4_out, counter_1_q, pull_resistor_1_node,
       register_1_q, register_2_q;

  Register #(.width(16)) register_1 (.D(Start), .en(1'b1), .clk(edgedetector_1_out_2), .Q(register_1_q));  // open: clr
  Register #(.width(16)) register_2 (.D(Steps), .en(1'b1), .clk(edgedetector_1_out_2), .Q(register_2_q));  // open: clr
  EdgeDetector edgedetector_1 (.in_1(AckPrev), .out_2(edgedetector_1_out_2));
  EdgeDetector edgedetector_2 (.in_1(ReqPost), .out_2(edgedetector_2_out_2));
  Pull_Resistor pull_resistor_1 (.node(pull_resistor_1_node));
  S_R_Flip_Flop s_r_ff_1 (.Q(s_r_ff_1_q), .reset(and_1_out), .preset(edgedetector_2_out_2));  // open: S, R, clk, Qn
  Counter #(.max('hffff), .width(16)) counter_1 (
    .clr(and_2_out), .up(1'b1), .count(not_1_out), .clk(Count), .D(pull_resistor_1_node), .Q(counter_1_q));  // open: load, carry
  not not_1 (not_1_out, PC_Fertig);
  not not_2 (not_2_out, PC_Fertig);
  not not_3 (not_3_out, Stop);
  and and_1 (and_1_out, not_2_out, not_3_out, s_r_ff_1_q);
  buf buffer_1 (buffer_1_out, and_1_out);
  buf buffer_2 (buffer_2_out, buffer_1_out);
  buf buffer_3 (buffer_3_out, buffer_2_out);
  buf buffer_4 (buffer_4_out, buffer_3_out);
  buf buffer_5 (buffer_5_out, buffer_4_out);
  buf buffer_6 (buffer_6_out, buffer_5_out);
  Adder #(.width(16)) adder_1 (.a(counter_1_q), .b(register_1_q), .out(adder_1_out));  // open: cin, cout
  buf buffer_7 (buffer_7_out, buffer_6_out);
  buf buffer_8 (buffer_8_out, buffer_7_out);
  buf buffer_9 (buffer_9_out, buffer_8_out);
  Comparator #(.mode("unsigned"), .width(16)) comparator_1 (
    .a(counter_1_q), .b(register_2_q), .eq(comparator_1_eq));  // open: gt, lt
  buf buffer_10 (buffer_10_out, buffer_9_out);
  buf buffer_11 (buffer_11_out, buffer_10_out);
  buf buffer_12 (buffer_12_out, buffer_11_out);
  buf buffer_13 (buffer_13_out, buffer_12_out);
  buf buffer_14 (buffer_14_out, buffer_13_out);
  and and_2 (and_2_out, Count, comparator_1_eq);
  buf buffer_15 (buffer_15_out, buffer_14_out);
  buf buffer_16 (buffer_16_out, buffer_15_out);
  buf buffer_17 (buffer_17_out, buffer_16_out);
  buf buffer_18 (buffer_18_out, buffer_17_out);
  buf buffer_19 (buffer_19_out, buffer_18_out);
  buf buffer_20 (buffer_20_out, buffer_19_out);
  S_R_Flip_Flop s_r_ff_2 (
    .Q(s_r_ff_2_q), .reset(and_2_out), .Qn(PC_Fertig), .preset(edgedetector_1_out_2));  // open: S, R, clk
  buf buffer_21 (buffer_21_out, buffer_20_out);
  buf buffer_22 (buffer_22_out, buffer_21_out);
  buf buffer_23 (buffer_23_out, buffer_22_out);
  buf buffer_24 (Count, buffer_23_out);
  T_Flip_Flop t_ff_1 (.T(1'b1), .clk(Count), .Q(t_ff_1_q));  // open: Qn, reset, preset
  buf buffer_25 (buffer_25_out, t_ff_1_q);
  buf buffer_26 (buffer_26_out, buffer_25_out);
  buf buffer_27 (buffer_27_out, buffer_26_out);
  Adder #(.width(16)) adder_2 (.a(adder_1_out), .b(16'h1), .out(adder_2_out));  // open: cin, cout
  Adder #(.width(16)) adder_3 (.a(adder_1_out), .b(16'h2), .out(adder_3_out));  // open: cin, cout
  Adder #(.width(16)) adder_4 (.a(adder_1_out), .b(16'h3), .out(adder_4_out));  // open: cin, cout
  buf buffer_28 (buffer_28_out, buffer_27_out);
  buf buffer_29 (buffer_29_out, buffer_28_out);
  buf buffer_30 (buffer_30_out, buffer_29_out);
  Register #(.width(16)) register_3 (.D(adder_1_out), .en(s_r_ff_2_q), .clk(Count), .Q(RAM1));  // open: clr
  Register #(.width(16)) register_4 (.D(adder_2_out), .en(s_r_ff_2_q), .clk(Count), .Q(RAM2));  // open: clr
  Register #(.width(16)) register_5 (.D(adder_3_out), .en(s_r_ff_2_q), .clk(Count), .Q(RAM3));  // open: clr
  Register #(.width(16)) register_6 (.D(adder_4_out), .en(s_r_ff_2_q), .clk(Count), .Q(RAM4));  // open: clr
  buf buffer_31 (buffer_31_out, buffer_30_out);
  buf buffer_32 (AckPost, buffer_31_out);
  T_Flip_Flop t_ff_2 (.T(1'b1), .clk(posedgedetector_1_out_2), .Q(ReqPrev));  // open: Qn, reset, preset
  PosEdgeDetector posedgedetector_1 (.in_1(PC_Fertig), .out_2(posedgedetector_1_out_2));
endmodule

module LSU (
  input  [7:0] AddrNr,
  input  [7:0] DeltaOffset,
  input  [7:0] Data_In,
  input  Pick,
  input  Add_Offset,
  input  Sub_Offset,
  input  ResetOffset,
  input  Write,
  input  Read,
  input  CLK,
  output [7:0] Bus_Out
);

  wire or_1_out, Reset1;
  wire [7:0] ram_1_dout, register_1_q;
  wire [15:0] adder_1_out, adder_2_out, multiplexer_1_out, multiplexer_2_out, OffsetTable_dout, rom_1_data,
       subtractor_1_out;

  Adder #(.width(16)) adder_1 (
    .a(OffsetTable_dout), .b({{8{1'b0}}, DeltaOffset}), .out(adder_1_out));  // open: cin, cout
  Subtractor #(.width(16)) subtractor_1 (
    .a(OffsetTable_dout), .b({{8{1'b0}}, DeltaOffset}), .out(subtractor_1_out));  // open: bin, bout
  D_Flip_Flop d_ff_1 (.D(ResetOffset), .clk(CLK), .Q(Reset1));  // open: Qn, preset, reset
  Register register_1 (.D(AddrNr), .en(Pick), .clk(CLK), .Q(register_1_q));  // open: clr
  or or_1 (or_1_out, Add_Offset, Sub_Offset, Reset1);
  Multiplexer #(.width(16)) multiplexer_1 (
    .in0(adder_1_out), .in1(subtractor_1_out), .out(multiplexer_1_out), .sel(Sub_Offset));
  Multiplexer #(.width(16)) multiplexer_2 (
    .in0(multiplexer_1_out), .in1({16{1'b0}}), .out(multiplexer_2_out), .sel(Reset1));
  RAM #(.dataWidth(16)) OffsetTable (
    .addr(register_1_q), .we(or_1_out), .oe(1'b1), .clk(CLK), .din(multiplexer_2_out), .dout(OffsetTable_dout));
  ROM #(.dataWidth(16)) rom_1 (.addr(register_1_q), .data(rom_1_data));
  Adder #(.width(16)) adder_2 (.a(OffsetTable_dout), .b(rom_1_data), .out(adder_2_out));  // open: cin, cout
  RAM #(.addrWidth(16)) ram_1 (.addr(adder_2_out), .we(Write), .oe(1'b1), .clk(CLK), .din(Data_In), .dout(ram_1_dout));
  Output_Unit output_unit_1 ();
  assign Bus_Out = Read ? ram_1_dout : 8'bz;  // Controlled_Buffer controlled_buffer_1

  // Other names for the same wires on the sheet: Add = Add_Offset; Reset = ResetOffset; Sub = Sub_Offset

  // Notes on the sheet:
  //   Position
  //   contents of rom_1 (hex, n*v repeats v):
  //   aa 12
  //   Offset Table
  //   Memory Address Table
  //   Data Out
endmodule

module ALU (
  input  [3:0] Funktion,
  input  [7:0] A,
  input  A_In,
  input  [7:0] B,
  input  B_In,
  input  C_Out,
  input  CLK,
  output [7:0] C
);

  wire [7:0] A_t, adder_1_out, adder_2_out, and_1_out, B_t, multiplexer_1_out, multiplier_1_out, not_1_out,
       or_1_out, shifter_1_out, subtractor_1_out, subtractor_2_out;

  assign A_t = A_In ? A : 8'bz;  // Controlled_Buffer controlled_buffer_1
  Pull_Resistor pull_resistor_1 (.node(A_t));
  assign B_t = B_In ? B : 8'bz;  // Controlled_Buffer controlled_buffer_2
  Pull_Resistor pull_resistor_2 (.node(B_t));
  Adder adder_1 (.a(A_t), .b(B_t), .out(adder_1_out));  // open: cin, cout
  Subtractor subtractor_1 (.a(A_t), .b(B_t), .out(subtractor_1_out));  // open: bin, bout
  Multiplier multiplier_1 (.a(A_t), .b(B_t), .out(multiplier_1_out));  // open: cin, cout
  Shifter shifter_1 (.in(A_t), .\dist (3'b001), .out(shifter_1_out));
  Adder adder_2 (.a(A_t), .b(8'h1), .out(adder_2_out));  // open: cin, cout
  Subtractor subtractor_2 (.a(A_t), .b(8'h1), .out(subtractor_2_out));  // open: bin, bout
  assign not_1_out = ~A_t;  // NOT_Gate not_1, 8 bits wide
  assign and_1_out = A_t & B_t;  // AND_Gate and_1, 8 bits wide
  assign or_1_out = A_t | B_t;  // OR_Gate or_1, 8 bits wide
  // Probe on adder_1_out
  Multiplexer #(.select(4), .width(8)) multiplexer_1 (
    .in0(adder_1_out), .in1(subtractor_1_out), .in2(multiplier_1_out), .in3(shifter_1_out),
    .in4(adder_2_out), .in5(subtractor_2_out), .in6(not_1_out), .in7(and_1_out), .in8(or_1_out),
    .out(multiplexer_1_out), .sel(Funktion));  // open: in9, in10, in11, in12, in13, in14, in15
  assign C = C_Out ? multiplexer_1_out : 8'bz;  // Controlled_Buffer controlled_buffer_3

  // Other names for the same wires on the sheet: Clock = CLK

  // Notes on the sheet:
  //   Beim Dividieren gibt es zwei Outputs
  //   Sie werden nacheinander auf den Belt geschrieben
  //   Aber Division ist mit TTL Logik zu aufwändig. Deshalb lasse ich es weg und mache es in Software
endmodule

module Instruction_Register (
  input  [7:0] Opcode_Byte,
  input  [7:0] OP1_Byte,
  input  [7:0] OP2_Byte,
  input  IR_In,
  input  CLK,
  output [7:0] Opcode,
  output [7:0] Operand1,
  output [7:0] Operand2
);

  Register register_1 (.D(Opcode_Byte), .en(IR_In), .clk(CLK), .Q(Opcode));  // open: clr
  Register register_2 (.D(OP1_Byte), .en(IR_In), .clk(CLK), .Q(Operand1));  // open: clr
  Register register_3 (.D(OP2_Byte), .en(IR_In), .clk(CLK), .Q(Operand2));  // open: clr
endmodule

module Belt (
  input  [7:0] R1,
  input  [7:0] R2,
  input  [7:0] Data_In,
  input  Write_Belt,
  input  CLK,
  output [7:0] R1_Data,
  output [7:0] R2_Data
);

  wire [7:0] multiplexer_1_out, multiplexer_2_out, register_1_q, register_2_q, register_3_q, register_4_q,
       register_5_q, register_6_q, register_7_q, register_8_q, register_9_q, register_10_q, register_11_q,
       register_12_q, register_13_q, register_14_q, register_15_q, register_16_q;

  Register register_1 (.D(Data_In), .en(Write_Belt), .clk(CLK), .Q(register_1_q));  // open: clr
  Register register_2 (.D(register_1_q), .en(Write_Belt), .clk(CLK), .Q(register_2_q));  // open: clr
  Register register_3 (.D(register_2_q), .en(Write_Belt), .clk(CLK), .Q(register_3_q));  // open: clr
  Register register_4 (.D(register_3_q), .en(Write_Belt), .clk(CLK), .Q(register_4_q));  // open: clr
  Register register_5 (.D(register_4_q), .en(Write_Belt), .clk(CLK), .Q(register_5_q));  // open: clr
  Register register_6 (.D(register_5_q), .en(Write_Belt), .clk(CLK), .Q(register_6_q));  // open: clr
  Register register_7 (.D(register_6_q), .en(Write_Belt), .clk(CLK), .Q(register_7_q));  // open: clr
  Register register_8 (.D(register_7_q), .en(Write_Belt), .clk(CLK), .Q(register_8_q));  // open: clr
  Register register_9 (.D(register_8_q), .en(Write_Belt), .clk(CLK), .Q(register_9_q));  // open: clr
  Register register_10 (.D(register_9_q), .en(Write_Belt), .clk(CLK), .Q(register_10_q));  // open: clr
  Register register_11 (.D(register_10_q), .en(Write_Belt), .clk(CLK), .Q(register_11_q));  // open: clr
  Register register_12 (.D(register_11_q), .en(Write_Belt), .clk(CLK), .Q(register_12_q));  // open: clr
  Register register_13 (.D(register_12_q), .en(Write_Belt), .clk(CLK), .Q(register_13_q));  // open: clr
  Register register_14 (.D(register_13_q), .en(Write_Belt), .clk(CLK), .Q(register_14_q));  // open: clr
  Register register_15 (.D(register_14_q), .en(Write_Belt), .clk(CLK), .Q(register_15_q));  // open: clr
  Register register_16 (.D(register_15_q), .en(Write_Belt), .clk(CLK), .Q(register_16_q));  // open: clr
  Multiplexer #(.select(4), .width(8)) multiplexer_1 (
    .in0(register_1_q), .in1(register_2_q), .in2(register_3_q), .in3(register_4_q), .in4(register_5_q),
    .in5(register_6_q), .in6(register_7_q), .in7(register_8_q), .in8(register_9_q), .in9(register_10_q),
    .in10(register_11_q), .in11(register_12_q), .in12(register_13_q), .in13(register_14_q),
    .in14(register_15_q), .in15(register_16_q), .out(multiplexer_1_out), .sel(R1[3:0]));
  Multiplexer #(.select(4), .width(8)) multiplexer_2 (
    .in0(register_1_q), .in1(register_2_q), .in2(register_3_q), .in3(register_4_q), .in4(register_5_q),
    .in5(register_6_q), .in6(register_7_q), .in7(register_8_q), .in8(register_9_q), .in9(register_10_q),
    .in10(register_11_q), .in11(register_12_q), .in12(register_13_q), .in13(register_14_q),
    .in14(register_15_q), .in15(register_16_q), .out(multiplexer_2_out), .sel(R2[3:0]));
  Register register_17 (.D(multiplexer_1_out), .en(1'b1), .clk(CLK), .Q(R1_Data));  // open: clr
  Register register_18 (.D(multiplexer_2_out), .en(1'b1), .clk(CLK), .Q(R2_Data));  // open: clr

  // Other names for the same wires on the sheet: WriteBelt = Write_Belt
endmodule

module ControlFlow_Unit (
  input  [2:0] Funktion,
  input  LU_F_In,
  input  [7:0] A,
  input  LU_A_In,
  input  [7:0] B,
  input  LU_B_In,
  input  If_Change_Bool,
  input  Elseif_Change_Bool,
  input  Else_Change_Bool,
  input  CLK,
  input  [7:0] Operand1,
  input  [7:0] Operand2,
  input  CheckCall,
  input  Check_CB_In,
  input  CheckBool,
  output [31:0] Codeblock,
  output [1:0] Call,
  output CodeBlock_In
);

  wire and_1_out, and_2_out, and_3_out, and_4_out, and_5_out, and_6_out, comparator_1_eq, comparator_2_eq,
       comparator_3_eq, comparator_4_gt, multiplexer_1_out, not_1_out, not_2_out, not_3_out, or_1_out,
       or_2_out, or_3_out, or_4_out, s_r_ff_1_q, s_r_ff_2_qn;
  wire [2:0] register_1_q;
  wire [7:0] A_t, B_t;

  Register #(.width(3)) register_1 (.D(Funktion), .en(LU_F_In), .clk(CLK), .Q(register_1_q));  // open: clr
  Register register_2 (.D(A), .en(LU_A_In), .clk(CLK), .Q(A_t));  // open: clr
  Register register_3 (.D(B), .en(LU_B_In), .clk(CLK), .Q(B_t));  // open: clr
  Comparator #(.mode("unsigned")) comparator_1 (.a(A_t), .b({8{1'b0}}), .eq(comparator_1_eq));  // open: gt, lt
  Comparator #(.mode("unsigned")) comparator_2 (.a(A_t), .b(8'h1), .eq(comparator_2_eq));  // open: gt, lt
  Comparator #(.mode("unsigned")) comparator_3 (.a(A_t), .b(B_t), .eq(comparator_3_eq));  // open: gt, lt
  Comparator #(.mode("unsigned")) comparator_4 (.a(A_t), .b(B_t), .gt(comparator_4_gt));  // open: eq, lt
  Multiplexer #(.select(3)) multiplexer_1 (
    .in0(comparator_1_eq), .in1(comparator_2_eq), .in2(comparator_3_eq), .in3(comparator_4_gt),
    .out(multiplexer_1_out), .sel(register_1_q));  // open: in4, in5, in6, in7
  and and_1 (and_1_out, Elseif_Change_Bool, multiplexer_1_out);
  and and_2 (and_2_out, multiplexer_1_out, If_Change_Bool);
  or or_1 (or_1_out, and_1_out, Else_Change_Bool);
  not not_1 (not_1_out, multiplexer_1_out);
  or or_2 (or_2_out, If_Change_Bool, Elseif_Change_Bool, Else_Change_Bool);
  and and_3 (and_3_out, or_2_out, not_2_out);
  not not_2 (not_2_out, or_3_out);
  or or_3 (or_3_out, and_2_out, and_4_out);
  and and_4 (and_4_out, or_1_out, s_r_ff_2_qn);
  and and_5 (and_5_out, CheckBool, s_r_ff_1_q);
  not not_3 (not_3_out, CheckBool);
  and and_6 (and_6_out, If_Change_Bool, not_1_out);
  S_R_Flip_Flop s_r_ff_1 (.S(or_3_out), .R(and_3_out), .clk(CLK), .Q(s_r_ff_1_q));  // open: reset, Qn, preset
  or or_4 (or_4_out, and_5_out, not_3_out);
  S_R_Flip_Flop s_r_ff_2 (.S(or_3_out), .R(and_6_out), .clk(CLK), .Qn(s_r_ff_2_qn));  // open: Q, reset, preset
  // AND_Gate and_7 has open pins: in0=CheckCall, in1=or_4_out, out=open
  and and_8 (CodeBlock_In, Check_CB_In, or_4_out);

  // Other names for the same wires on the sheet: Else_Change = Else_Change_Bool; Elseif_Change = Elseif_Change_Bool;
  //   If_Change = If_Change_Bool

  // Notes on the sheet:
  //   F kommt von der CU
  //   0: A=0
  //   1: A=1
  //   2: A=B
  //   3: A>B
  //   Call darf frühestens hier stattfinden. Es könnte immer einen CPush geben
  //   Calls/Pushs müssen alle hier stattfinden, damit die Reihenfolge nicht vertauscht wird
  //   Gab es schon ein True?
  //   Boolean
endmodule

module Instruction_Decoder (
  input  [47:0] Instruction,
  output [63:0] Signals_Out,
  output [7:0] OP1,
  output [7:0] OP2,
  output If_Change,
  output Elseif_Change,
  output Else_Change,
  output [2:0] LU_F,
  output LU_F_In,
  output LU_A_In,
  output LU_B_In,
  output LSU_Pick,
  output LSU_Add_Offset,
  output LSU_Sub_Offset,
  output LSU_Reset_Offset,
  output WriteMemory,
  output ReadMemory,
  output [3:0] ALU_F,
  output ALU_A_In,
  output ALU_B_In,
  output ALU_C_Out,
  output Call,
  output CodeBlock_IN,
  output Pass_Immediate,
  output CheckBool,
  output Pass_Data1,
  output Read_Scratchpad,
  output Write_Scratchpad,
  output AckPrev
);

  wire Ack_ID, AddRegIndOffset, ALU_A_In_t, ALU_B_In_t, ALU_C_Out_t, Call_t, CheckBool_t, CLK,
       CodeBlock_IN_t, drailbytereceiver_1_allchanged, drailbytereceiver_2_allchanged, Else_Change_t,
       Elseif_Change_t, If_Change_t, Load, LSU_Add_Offset_t, LSU_Pick_t, LSU_Reset_Offset_t,
       LSU_Sub_Offset_t, LU_A_In_t, LU_B_In_t, LU_F_In_t, opcodedecoder_1_abiggerb, opcodedecoder_1_add,
       opcodedecoder_1_aeq0, opcodedecoder_1_aeq1, opcodedecoder_1_aeqb, opcodedecoder_1_bitshift,
       opcodedecoder_1_callblock, opcodedecoder_1_ccall, opcodedecoder_1_cpush, opcodedecoder_1_decrement,
       opcodedecoder_1_fill, opcodedecoder_1_immediate, opcodedecoder_1_increment, opcodedecoder_1_logand,
       opcodedecoder_1_lognot, opcodedecoder_1_logor, opcodedecoder_1_multiply, opcodedecoder_1_pushblock,
       opcodedecoder_1_renew, opcodedecoder_1_spill, opcodedecoder_1_subtract, or_1_out, Pass_Data1_t,
       Pass_Immediate_t, PickAddr, PickAddrResetOffset, Read_Memory, Read_Scratchpad_t, Store,
       SubRegIndOffset, undriven, Write_Belt, Write_Memory, Write_Scratchpad_t;
  wire [2:0] LU_F_t;
  wire [3:0] ALU_F_t;
  wire [7:0] Direct_Out, drailbytereceiver_1_byte, R2_Out;
  wire [28:0] undriven_2;

  DRailByteReceiver drailbytereceiver_1 (
    .ReadyDelay(Ack_ID), .DualRailByte(Instruction[47:32]), .OtherBytesChanged(1'b1),
    .AllChanged(drailbytereceiver_1_allchanged), .Byte(drailbytereceiver_1_byte));  // open: Stop, DelayStart, Acknowledge
  DRailByteReceiver drailbytereceiver_2 (
    .ReadyDelay(Ack_ID), .DualRailByte(Instruction[31:16]),
    .OtherBytesChanged(drailbytereceiver_1_allchanged), .AllChanged(drailbytereceiver_2_allchanged),
    .Byte(Direct_Out));  // open: Stop, DelayStart, Acknowledge
  DRailByteReceiver drailbytereceiver_3 (
    .ReadyDelay(Ack_ID), .DualRailByte(Instruction[15:0]),
    .OtherBytesChanged(drailbytereceiver_2_allchanged), .Acknowledge(AckPrev), .Byte(R2_Out));  // open: Stop, DelayStart, AllChanged
  // Probe on drailbytereceiver_1_byte
  OpcodeDecoder opcodedecoder_1 (
    .Instruction(drailbytereceiver_1_byte), .Gueltig(undriven), .Immediate(opcodedecoder_1_immediate),
    .CallBlock(opcodedecoder_1_callblock), .PushBlock(opcodedecoder_1_pushblock),
    .CCall(opcodedecoder_1_ccall), .CPush(opcodedecoder_1_cpush), .Aeq0(opcodedecoder_1_aeq0),
    .Aeq1(opcodedecoder_1_aeq1), .AeqB(opcodedecoder_1_aeqb), .AbiggerB(opcodedecoder_1_abiggerb),
    .IF_Bool(If_Change_t), .ELSEIF_Bool(Elseif_Change_t), .ELSE_Bool(Else_Change_t),
    .Renew(opcodedecoder_1_renew), .Spill(opcodedecoder_1_spill), .Fill(opcodedecoder_1_fill),
    .PickAddr(PickAddr), .PickAddrResetOffset(PickAddrResetOffset), .Load(Load), .Store(Store),
    .AddRegIndOffset(AddRegIndOffset), .SubRegIndOffset(SubRegIndOffset), .Add(opcodedecoder_1_add),
    .Subtract(opcodedecoder_1_subtract), .Multiply(opcodedecoder_1_multiply),
    .BitShift(opcodedecoder_1_bitshift), .Increment(opcodedecoder_1_increment),
    .Decrement(opcodedecoder_1_decrement), .LogNot(opcodedecoder_1_lognot), .LogAnd(opcodedecoder_1_logand),
    .LogOr(opcodedecoder_1_logor));  // open: NOP
  or or_1 (or_1_out, opcodedecoder_1_add, opcodedecoder_1_subtract, opcodedecoder_1_multiply, opcodedecoder_1_bitshift, opcodedecoder_1_increment, opcodedecoder_1_decrement, opcodedecoder_1_lognot, opcodedecoder_1_logand, opcodedecoder_1_logor);
  assign ALU_A_In_t = or_1_out ? 1'b1 : 1'bz;  // Controlled_Buffer controlled_buffer_1
  assign ALU_B_In_t = or_1_out ? 1'b1 : 1'bz;  // Controlled_Buffer controlled_buffer_2
  assign Write_Belt = or_1_out ? 1'b1 : 1'bz;  // Controlled_Buffer controlled_buffer_3
  assign ALU_C_Out_t = or_1_out ? 1'b1 : 1'bz;  // Controlled_Buffer controlled_buffer_4
  Pull_Resistor pull_resistor_1 (.node(or_1_out));
  assign ALU_F_t = opcodedecoder_1_add ? 4'b0000 : 4'bz;  // Controlled_Buffer controlled_buffer_5
  assign ALU_F_t = opcodedecoder_1_subtract ? 4'b0001 : 4'bz;  // Controlled_Buffer controlled_buffer_6
  assign ALU_F_t = opcodedecoder_1_multiply ? 4'b0010 : 4'bz;  // Controlled_Buffer controlled_buffer_7
  assign ALU_F_t = opcodedecoder_1_bitshift ? 4'b0011 : 4'bz;  // Controlled_Buffer controlled_buffer_8
  assign ALU_F_t = opcodedecoder_1_increment ? 4'b1100 : 4'bz;  // Controlled_Buffer controlled_buffer_9
  assign ALU_F_t = opcodedecoder_1_decrement ? 4'b1101 : 4'bz;  // Controlled_Buffer controlled_buffer_10
  assign ALU_F_t = opcodedecoder_1_lognot ? 4'b1110 : 4'bz;  // Controlled_Buffer controlled_buffer_11
  assign ALU_F_t = opcodedecoder_1_logand ? 4'b1111 : 4'bz;  // Controlled_Buffer controlled_buffer_12
  Pull_Resistor pull_resistor_2 (.node(ALU_F_t));
  assign ALU_F_t = opcodedecoder_1_logor ? 4'b0000 : 4'bz;  // Controlled_Buffer controlled_buffer_13
  Pull_Resistor pull_resistor_3 (.node(ALU_A_In_t));
  Pull_Resistor pull_resistor_4 (.node(ALU_B_In_t));
  Pull_Resistor pull_resistor_5 (.node(Write_Belt));
  Pull_Resistor pull_resistor_6 (.node(ALU_C_Out_t));
  Pull_Resistor pull_resistor_7 (.node(Call_t));
  assign Call_t = opcodedecoder_1_callblock ? 1'b1 : 1'bz;  // Controlled_Buffer controlled_buffer_14
  assign CodeBlock_IN_t = opcodedecoder_1_callblock ? 1'b1 : 1'bz;  // Controlled_Buffer controlled_buffer_15
  Pull_Resistor pull_resistor_8 (.node(opcodedecoder_1_callblock));
  assign CodeBlock_IN_t = opcodedecoder_1_pushblock ? 1'b1 : 1'bz;  // Controlled_Buffer controlled_buffer_16
  Pull_Resistor pull_resistor_9 (.node(opcodedecoder_1_pushblock));
  Pull_Resistor pull_resistor_10 (.node(CodeBlock_IN_t));
  assign CheckBool_t = opcodedecoder_1_ccall ? 1'b1 : 1'bz;  // Controlled_Buffer controlled_buffer_17
  assign Call_t = opcodedecoder_1_ccall ? 1'b1 : 1'bz;  // Controlled_Buffer controlled_buffer_18
  assign CodeBlock_IN_t = opcodedecoder_1_ccall ? 1'b1 : 1'bz;  // Controlled_Buffer controlled_buffer_19
  Pull_Resistor pull_resistor_11 (.node(opcodedecoder_1_ccall));
  Pull_Resistor pull_resistor_12 (.node(CheckBool_t));
  assign CheckBool_t = opcodedecoder_1_cpush ? 1'b1 : 1'bz;  // Controlled_Buffer controlled_buffer_20
  assign CodeBlock_IN_t = opcodedecoder_1_cpush ? 1'b1 : 1'bz;  // Controlled_Buffer controlled_buffer_21
  Pull_Resistor pull_resistor_13 (.node(opcodedecoder_1_cpush));
  Pull_Resistor pull_resistor_14 (.node(LU_F_t));
  assign LU_F_t = opcodedecoder_1_aeqb ? 3'b010 : 3'bz;  // Controlled_Buffer controlled_buffer_22
  assign LU_F_In_t = opcodedecoder_1_aeqb ? 1'b1 : 1'bz;  // Controlled_Buffer controlled_buffer_23
  assign LU_A_In_t = opcodedecoder_1_aeqb ? 1'b1 : 1'bz;  // Controlled_Buffer controlled_buffer_24
  assign LU_B_In_t = opcodedecoder_1_aeqb ? 1'b1 : 1'bz;  // Controlled_Buffer controlled_buffer_25
  Pull_Resistor pull_resistor_15 (.node(opcodedecoder_1_aeqb));
  Pull_Resistor pull_resistor_16 (.node(LU_F_In_t));
  Pull_Resistor pull_resistor_17 (.node(LU_A_In_t));
  Pull_Resistor pull_resistor_18 (.node(LU_B_In_t));
  Pull_Resistor pull_resistor_19 (.node(opcodedecoder_1_abiggerb));
  assign LU_F_t = opcodedecoder_1_abiggerb ? 3'b011 : 3'bz;  // Controlled_Buffer controlled_buffer_26
  assign LU_F_In_t = opcodedecoder_1_abiggerb ? 1'b1 : 1'bz;  // Controlled_Buffer controlled_buffer_27
  Pull_Resistor pull_resistor_20 (.node(LU_F_In_t));
  assign LU_A_In_t = opcodedecoder_1_abiggerb ? 1'b1 : 1'bz;  // Controlled_Buffer controlled_buffer_28
  Pull_Resistor pull_resistor_21 (.node(LU_A_In_t));
  assign LU_B_In_t = opcodedecoder_1_abiggerb ? 1'b1 : 1'bz;  // Controlled_Buffer controlled_buffer_29
  Pull_Resistor pull_resistor_22 (.node(LU_B_In_t));
  assign LU_F_t = opcodedecoder_1_aeq0 ? 3'b000 : 3'bz;  // Controlled_Buffer controlled_buffer_30
  assign LU_F_In_t = opcodedecoder_1_aeq0 ? 1'b1 : 1'bz;  // Controlled_Buffer controlled_buffer_31
  Pull_Resistor pull_resistor_23 (.node(LU_F_In_t));
  assign LU_A_In_t = opcodedecoder_1_aeq0 ? 1'b1 : 1'bz;  // Controlled_Buffer controlled_buffer_32
  Pull_Resistor pull_resistor_24 (.node(opcodedecoder_1_aeq0));
  Pull_Resistor pull_resistor_25 (.node(LU_A_In_t));
  assign LU_F_t = opcodedecoder_1_aeq1 ? 3'b001 : 3'bz;  // Controlled_Buffer controlled_buffer_33
  assign LU_F_In_t = opcodedecoder_1_aeq1 ? 1'b1 : 1'bz;  // Controlled_Buffer controlled_buffer_34
  assign LU_A_In_t = opcodedecoder_1_aeq1 ? 1'b1 : 1'bz;  // Controlled_Buffer controlled_buffer_35
  Pull_Resistor pull_resistor_26 (.node(opcodedecoder_1_aeq1));
  Pull_Resistor pull_resistor_27 (.node(LU_F_In_t));
  Pull_Resistor pull_resistor_28 (.node(LU_A_In_t));
  assign Write_Belt = opcodedecoder_1_renew ? 1'b1 : 1'bz;  // Controlled_Buffer controlled_buffer_36
  assign Pass_Data1_t = opcodedecoder_1_renew ? 1'b1 : 1'bz;  // Controlled_Buffer controlled_buffer_37
  Pull_Resistor pull_resistor_29 (.node(Write_Belt));
  Pull_Resistor pull_resistor_30 (.node(Pass_Data1_t));
  assign Write_Scratchpad_t = opcodedecoder_1_spill ? 1'b1 : 1'bz;  // Controlled_Buffer controlled_buffer_38
  Pull_Resistor pull_resistor_31 (.node(Write_Scratchpad_t));
  assign Write_Belt = opcodedecoder_1_fill ? 1'b1 : 1'bz;  // Controlled_Buffer controlled_buffer_39
  assign Read_Scratchpad_t = opcodedecoder_1_fill ? 1'b1 : 1'bz;  // Controlled_Buffer controlled_buffer_40
  Pull_Resistor pull_resistor_32 (.node(Write_Belt));
  Pull_Resistor pull_resistor_33 (.node(Read_Scratchpad_t));
  assign Write_Belt = opcodedecoder_1_immediate ? 1'b1 : 1'bz;  // Controlled_Buffer controlled_buffer_41
  assign Pass_Immediate_t = opcodedecoder_1_immediate ? 1'b1 : 1'bz;  // Controlled_Buffer controlled_buffer_42
  Pull_Resistor pull_resistor_34 (.node(opcodedecoder_1_immediate));
  Pull_Resistor pull_resistor_35 (.node(Write_Belt));
  Pull_Resistor pull_resistor_36 (.node(Pass_Immediate_t));
  Pull_Resistor pull_resistor_37 (.node(Load));
  Pull_Resistor pull_resistor_38 (.node(Store));
  Pull_Resistor pull_resistor_39 (.node(PickAddrResetOffset));
  Pull_Resistor pull_resistor_40 (.node(AddRegIndOffset));
  Pull_Resistor pull_resistor_41 (.node(SubRegIndOffset));
  Pull_Resistor pull_resistor_42 (.node(PickAddr));
  assign Write_Belt = Load ? 1'b1 : 1'bz;  // Controlled_Buffer controlled_buffer_43
  Pull_Resistor pull_resistor_43 (.node(Write_Belt));
  assign Read_Memory = Load ? 1'b1 : 1'bz;  // Controlled_Buffer controlled_buffer_44
  Pull_Resistor pull_resistor_44 (.node(Read_Memory));
  assign Write_Memory = Store ? 1'b1 : 1'bz;  // Controlled_Buffer controlled_buffer_45
  Pull_Resistor pull_resistor_45 (.node(Write_Memory));
  assign LSU_Pick_t = PickAddrResetOffset ? 1'b1 : 1'bz;  // Controlled_Buffer controlled_buffer_46
  Pull_Resistor pull_resistor_46 (.node(LSU_Pick_t));
  assign LSU_Reset_Offset_t = PickAddrResetOffset ? 1'b1 : 1'bz;  // Controlled_Buffer controlled_buffer_47
  Pull_Resistor pull_resistor_47 (.node(LSU_Reset_Offset_t));
  assign LSU_Add_Offset_t = AddRegIndOffset ? 1'b1 : 1'bz;  // Controlled_Buffer controlled_buffer_48
  Pull_Resistor pull_resistor_48 (.node(LSU_Add_Offset_t));
  assign LSU_Sub_Offset_t = SubRegIndOffset ? 1'b1 : 1'bz;  // Controlled_Buffer controlled_buffer_49
  Pull_Resistor pull_resistor_49 (.node(LSU_Sub_Offset_t));
  assign LSU_Pick_t = PickAddr ? 1'b1 : 1'bz;  // Controlled_Buffer controlled_buffer_50
  Pull_Resistor pull_resistor_50 (.node(LSU_Pick_t));
  Register #(.width(64)) ExecuteBuffer (
    .D({Direct_Out, R2_Out, If_Change_t, Elseif_Change_t, Else_Change_t, LU_F_t, LU_F_In_t, LU_A_In_t, LU_B_In_t, LSU_Pick_t, LSU_Add_Offset_t, LSU_Sub_Offset_t, LSU_Reset_Offset_t, Write_Memory, Read_Memory, ALU_F_t, undriven_2[28:27], ALU_A_In_t, ALU_B_In_t, ALU_C_Out_t, undriven_2[23:22], Call_t, CodeBlock_IN_t, Write_Belt, Pass_Immediate_t, CheckBool_t, Pass_Data1_t, Read_Scratchpad_t, Write_Scratchpad_t, undriven_2[13:0]}),
    .en(1'b1), .clk(CLK),
    .Q({OP1, OP2, If_Change, Elseif_Change, Else_Change, LU_F, LU_F_In, LU_A_In, LU_B_In, LSU_Pick, LSU_Add_Offset, LSU_Sub_Offset, LSU_Reset_Offset, Signals_Out[34], ReadMemory, ALU_F, Signals_Out[28:27], ALU_A_In, ALU_B_In, ALU_C_Out, Signals_Out[23:22], Call, CodeBlock_IN, Signals_Out[19], Pass_Immediate, CheckBool, Pass_Data1, Read_Scratchpad, Signals_Out[14:0]}));  // open: clr

  assign {Signals_Out[63:35], Signals_Out[33:29], Signals_Out[26:24], Signals_Out[21:20], Signals_Out[18:15]} = {OP1, OP2, If_Change, Elseif_Change, Else_Change, LU_F, LU_F_In, LU_A_In, LU_B_In, LSU_Pick, LSU_Add_Offset, LSU_Sub_Offset, LSU_Reset_Offset, ReadMemory, ALU_F, ALU_A_In, ALU_B_In, ALU_C_Out, Call, CodeBlock_IN, Pass_Immediate, CheckBool, Pass_Data1, Read_Scratchpad};
  assign Write_Scratchpad = Signals_Out[14];
  assign WriteMemory = Signals_Out[34];

  // Other names for the same wires on the sheet: R1_Out[7:0] = Direct_Out

  // Notes on the sheet:
  //   01 = Call
  //   02 = Push
  //   03 = CCall
  //   04 = CPush
  //   07 = A=B
  //   08 = A>B
  //   05 = A=0
  //   06 = A=1
endmodule

module Injector (
  input  Beginn,
  input  [15:0] Start_CodeBlock,
  input  [31:0] CodeBlock_IN,
  input  [1:0] Call_or_Push,
  input  Stop,
  input  Acknowledge,
  output [31:0] CodeBlock_OUT,
  output [1:0] Call_or_Push_OUT,
  output AckPrev
);

  wire drailbitreceiverfull_1_bit, drailbitreceiverfull_1_delaystart, drailbytereceiver_1_allchanged,
       drailbytereceiver_2_allchanged, drailbytesender_1_fertig, edgedetector_1_out_2, multiplexer_2_out,
       or_1_out, posedgedetector_1_out_2, posedgedetector_2_out_2, s_r_ff_1_q, t_ff_1_q;
  wire [7:0] drailbytereceiver_1_byte, drailbytereceiver_2_byte;
  wire [15:0] multiplexer_1_out;

  // Probe on CodeBlock_IN
  DRailByteReceiver drailbytereceiver_1 (
    .Stop(Stop), .ReadyDelay(Acknowledge), .DualRailByte(CodeBlock_IN[31:16]), .OtherBytesChanged(1'b1),
    .AllChanged(drailbytereceiver_1_allchanged), .Byte(drailbytereceiver_1_byte));  // open: DelayStart, Acknowledge
  DRailByteReceiver drailbytereceiver_2 (
    .Stop(Stop), .ReadyDelay(Acknowledge), .DualRailByte(CodeBlock_IN[15:0]),
    .OtherBytesChanged(drailbytereceiver_1_allchanged), .AllChanged(drailbytereceiver_2_allchanged),
    .Byte(drailbytereceiver_2_byte));  // open: DelayStart, Acknowledge
  DRailBitReceiverFull drailbitreceiverfull_1 (
    .Stop(Stop), .ReadyDelay(Acknowledge), .DualRailBit(Call_or_Push),
    .OtherBytesChanged(drailbytereceiver_2_allchanged), .DelayStart(drailbitreceiverfull_1_delaystart),
    .Acknowledge(AckPrev), .Bit(drailbitreceiverfull_1_bit));  // open: AllChanged
  PosEdgeDetector posedgedetector_1 (.in_1(Beginn), .out_2(posedgedetector_1_out_2));
  S_R_Flip_Flop s_r_ff_1 (
    .Q(s_r_ff_1_q), .reset(posedgedetector_2_out_2), .preset(posedgedetector_1_out_2));  // open: S, R, clk, Qn
  EdgeDetector edgedetector_1 (.in_1(drailbitreceiverfull_1_delaystart), .out_2(edgedetector_1_out_2));
  // Probe on multiplexer_1_out
  Multiplexer #(.width(16)) multiplexer_1 (
    .in0({drailbytereceiver_1_byte, drailbytereceiver_2_byte}), .in1(Start_CodeBlock),
    .out(multiplexer_1_out), .sel(s_r_ff_1_q));
  Multiplexer multiplexer_2 (.in0(drailbitreceiverfull_1_bit), .in1(1'b1), .out(multiplexer_2_out), .sel(s_r_ff_1_q));
  T_Flip_Flop t_ff_1 (.T(1'b1), .clk(or_1_out), .Q(t_ff_1_q));  // open: Qn, reset, preset
  or or_1 (or_1_out, s_r_ff_1_q, edgedetector_1_out_2);
  DRailByteSender drailbytesender_1 (
    .Acknowledge(Acknowledge), .Request(t_ff_1_q), .Byte(multiplexer_1_out[7:0]),
    .Fertig(drailbytesender_1_fertig), .DualRailByte(CodeBlock_OUT[15:0]));
  DRailByteSender drailbytesender_2 (
    .Acknowledge(Acknowledge), .Request(t_ff_1_q), .Byte(multiplexer_1_out[15:8]),
    .DualRailByte(CodeBlock_OUT[31:16]));  // open: Fertig
  DRailBitSenderFull drailbitsenderfull_1 (
    .Acknowledge(Acknowledge), .Request(t_ff_1_q), .Bit(multiplexer_2_out), .DualRailBit(Call_or_Push_OUT));  // open: Fertig
  // Probe on CodeBlock_OUT
  PosEdgeDetector posedgedetector_2 (.in_1(drailbytesender_1_fertig), .out_2(posedgedetector_2_out_2));

  // Other names for the same wires on the sheet: Ack = Acknowledge
endmodule

module OpcodeDecoder (
  input  [7:0] Instruction,
  input  Gueltig,
  output NOP,
  output Immediate,
  output CallBlock,
  output PushBlock,
  output CCall,
  output CPush,
  output Aeq0,
  output Aeq1,
  output AeqB,
  output AbiggerB,
  output IF_Bool,
  output ELSEIF_Bool,
  output ELSE_Bool,
  output Renew,
  output Spill,
  output Fill,
  output PickAddr,
  output PickAddrResetOffset,
  output Load,
  output Store,
  output AddRegIndOffset,
  output SubRegIndOffset,
  output Add,
  output Subtract,
  output Multiply,
  output BitShift,
  output Increment,
  output Decrement,
  output LogNot,
  output LogAnd,
  output LogOr
);

  // Probe on Instruction
  Demultiplexer #(.select(5)) demultiplexer_1 (
    .out0(NOP), .out1(Immediate), .out2(CallBlock), .out3(PushBlock), .out4(CCall), .out5(CPush),
    .out6(Aeq0), .out7(Aeq1), .out8(AeqB), .out9(AbiggerB), .out10(IF_Bool), .out11(ELSEIF_Bool),
    .out12(ELSE_Bool), .out13(Renew), .out14(Spill), .out15(Fill), .out16(PickAddr),
    .out17(PickAddrResetOffset), .out18(Load), .out19(Store), .out20(AddRegIndOffset),
    .out21(SubRegIndOffset), .out22(Add), .out23(Subtract), .out24(Multiply), .out25(BitShift),
    .out26(Increment), .out27(Decrement), .out28(LogNot), .out29(LogAnd), .out30(LogOr), .in(Gueltig),
    .sel(Instruction[4:0]));  // open: out31
endmodule

module Execute_Buffer (
  input  [63:0] ControlSignals,
  input  CLK,
  input  [7:0] Data1_In,
  input  [7:0] Data2_In,
  output [63:0] Signals_Out,
  output [7:0] OP1,
  output [7:0] OP2,
  output If_Change,
  output Elseif_Change,
  output Else_Change,
  output [2:0] LU_F,
  output LU_F_In,
  output LU_A_In,
  output LU_B_In,
  output LSU_Pos_In,
  output LSU_Add_Offset,
  output LSU_Reset_Offset,
  output Write_Memory,
  output Read_Memory,
  output [2:0] ALU_F,
  output ALU_F_In,
  output Reg_Addr_In,
  output Reg_Read,
  output Reg_Write,
  output ALU_A_In,
  output ALU_B_In,
  output ALU_C_Out,
  output ALU_R_Out,
  output PC_Enable,
  output Call,
  output CodeBlock_IN,
  output Write_Belt,
  output Pass_Immediate,
  output CheckBool,
  output Pass_Data1,
  output Read_Scratchpad,
  output Write_Scratchpad,
  output [7:0] Data1_Out,
  output [7:0] Data2_Out
);

  Register #(.width(64)) register_1 (
    .D(ControlSignals), .en(1'b1), .clk(CLK),
    .Q({OP1, OP2, If_Change, Elseif_Change, Else_Change, LU_F, LU_F_In, LU_A_In, LU_B_In, LSU_Pos_In, LSU_Add_Offset, LSU_Reset_Offset, Signals_Out[35], Read_Memory, ALU_F, ALU_F_In, Reg_Addr_In, Reg_Read, Reg_Write, ALU_A_In, ALU_B_In, ALU_C_Out, ALU_R_Out, PC_Enable, Call, CodeBlock_IN, Signals_Out[19], Pass_Immediate, CheckBool, Pass_Data1, Read_Scratchpad, Signals_Out[14:0]}));  // open: clr
  Register register_2 (.D(Data1_In), .en(1'b1), .clk(CLK), .Q(Data1_Out));  // open: clr
  Register register_3 (.D(Data2_In), .en(1'b1), .clk(CLK), .Q(Data2_Out));  // open: clr

  assign {Signals_Out[63:36], Signals_Out[34:20], Signals_Out[18:15]} = {OP1, OP2, If_Change, Elseif_Change, Else_Change, LU_F, LU_F_In, LU_A_In, LU_B_In, LSU_Pos_In, LSU_Add_Offset, LSU_Reset_Offset, Read_Memory, ALU_F, ALU_F_In, Reg_Addr_In, Reg_Read, Reg_Write, ALU_A_In, ALU_B_In, ALU_C_Out, ALU_R_Out, PC_Enable, Call, CodeBlock_IN, Pass_Immediate, CheckBool, Pass_Data1, Read_Scratchpad};
  assign Write_Belt = Signals_Out[19];
  assign Write_Memory = Signals_Out[35];
  assign Write_Scratchpad = Signals_Out[14];
endmodule

module Scratchpad (
  input  [7:0] Data_In,
  input  [7:0] Addr,
  input  Write,
  input  Read,
  input  CLK,
  output [7:0] Data_Out
);

  wire [7:0] ram_1_dout;

  RAM ram_1 (.addr(Addr), .we(Write), .oe(1'b1), .clk(CLK), .din(Data_In), .dout(ram_1_dout));
  assign Data_Out = Read ? ram_1_dout : 8'bz;  // Controlled_Buffer controlled_buffer_1
endmodule

module WB_Buffer (
  input  [63:0] ControlSignals,
  input  CLK,
  input  [7:0] WB_Data_In,
  output [63:0] Signals_Out,
  output Write_Belt,
  output [7:0] WB_Data_Out
);

  Register #(.width(64)) register_1 (.D(ControlSignals), .en(1'b1), .clk(CLK), .Q(Signals_Out));  // open: clr
  Register register_2 (.D(WB_Data_In), .en(1'b1), .clk(CLK), .Q(WB_Data_Out));  // open: clr

  assign Write_Belt = Signals_Out[19];
endmodule

module InstructionLengthDecoder (
  input  [7:0] Byte_1,
  input  [7:0] Byte_2,
  input  [7:0] Byte_3,
  input  [7:0] Byte_4,
  input  PC_Fertig,
  input  CLK,
  output [7:0] Opcode,
  output [7:0] Operand1,
  output [7:0] Operand2,
  output Valid,
  output PC_Enable
);

  wire adder_2_cout, and_1_out, and_2_out, and_3_out, and_4_out, and_5_out, and_6_out, and_7_out, and_8_out,
       and_9_out, and_10_out, and_11_out, comparator_1_eq, comparator_2_eq, comparator_3_eq, comparator_4_eq,
       d_ff_1_qn, d_ff_2_q, d_ff_2_qn, dreiBytes, minimalopcodedecoder_1_einbyte,
       minimalopcodedecoder_1_zweibytes, not_1_out, not_3_out, or_2_out, zweiBytes;
  wire [1:0] adder_1_out, controlled_buffer_1_out, register_1_q, subtractor_1_out;
  wire [7:0] controlled_buffer_4_out, controlled_buffer_8_out, controlled_buffer_12_out, FrameBuffer_q,
       multiplexer_1_out, register_2_q, register_3_q, register_4_q;

  MinimalOpcodeDecoder minimalopcodedecoder_1 (
    .Instruction(multiplexer_1_out), .einByte(minimalopcodedecoder_1_einbyte),
    .zweiBytes(minimalopcodedecoder_1_zweibytes), .dreiBytes(dreiBytes));
  assign controlled_buffer_1_out = minimalopcodedecoder_1_einbyte ? 2'b01 : 2'bz;  // Controlled_Buffer controlled_buffer_1
  assign controlled_buffer_1_out = minimalopcodedecoder_1_zweibytes ? 2'b10 : 2'bz;  // Controlled_Buffer controlled_buffer_2
  assign controlled_buffer_1_out = dreiBytes ? 2'b11 : 2'bz;  // Controlled_Buffer controlled_buffer_3
  Pull_Resistor pull_resistor_1 (.node(controlled_buffer_1_out));
  Adder #(.width(2)) adder_1 (.a(register_1_q), .b(controlled_buffer_1_out), .out(adder_1_out));  // open: cin, cout
  not not_1 (not_1_out, PC_Fertig);
  Register #(.width(2)) register_1 (.D(adder_1_out), .en(Valid), .clk(CLK), .Q(register_1_q));  // open: clr
  and and_1 (and_1_out, not_1_out, PC_Enable);
  Register FrameBuffer (.D(Byte_1), .en(and_1_out), .clk(CLK), .Q(FrameBuffer_q));  // open: clr
  Register register_2 (.D(Byte_2), .en(and_1_out), .clk(CLK), .Q(register_2_q));  // open: clr
  Register register_3 (.D(Byte_3), .en(and_1_out), .clk(CLK), .Q(register_3_q));  // open: clr
  Register register_4 (.D(Byte_4), .en(and_1_out), .clk(CLK), .Q(register_4_q));  // open: clr
  Subtractor #(.width(2)) subtractor_1 (
    .a(controlled_buffer_1_out), .b(2'b01), .out(subtractor_1_out));  // open: bin, bout
  Comparator #(.mode("unsigned"), .width(2)) comparator_1 (
    .a(2'b00), .b(register_1_q), .eq(comparator_1_eq));  // open: gt, lt
  Comparator #(.mode("unsigned"), .width(2)) comparator_2 (
    .a(2'b01), .b(register_1_q), .eq(comparator_2_eq));  // open: gt, lt
  Comparator #(.mode("unsigned"), .width(2)) comparator_3 (
    .a(2'b10), .b(register_1_q), .eq(comparator_3_eq));  // open: gt, lt
  Comparator #(.mode("unsigned"), .width(2)) comparator_4 (
    .a(2'b11), .b(register_1_q), .eq(comparator_4_eq));  // open: gt, lt
  Adder #(.width(2)) adder_2 (.a(register_1_q), .b(subtractor_1_out), .cout(adder_2_cout));  // open: out, cin
  or or_1 (zweiBytes, dreiBytes, minimalopcodedecoder_1_zweibytes);
  and and_2 (and_2_out, comparator_1_eq, zweiBytes);
  and and_3 (and_3_out, comparator_2_eq, zweiBytes);
  and and_4 (and_4_out, comparator_3_eq, zweiBytes);
  and and_5 (and_5_out, comparator_4_eq, zweiBytes);
  assign controlled_buffer_4_out = comparator_1_eq ? FrameBuffer_q : 8'bz;  // Controlled_Buffer controlled_buffer_4
  assign controlled_buffer_4_out = comparator_2_eq ? register_2_q : 8'bz;  // Controlled_Buffer controlled_buffer_5
  assign controlled_buffer_4_out = comparator_3_eq ? register_3_q : 8'bz;  // Controlled_Buffer controlled_buffer_6
  assign controlled_buffer_4_out = comparator_4_eq ? register_4_q : 8'bz;  // Controlled_Buffer controlled_buffer_7
  Pull_Resistor pull_resistor_2 (.node(controlled_buffer_4_out));
  and and_6 (and_6_out, and_2_out, dreiBytes);
  and and_7 (and_7_out, and_3_out, dreiBytes);
  and and_8 (and_8_out, and_4_out, dreiBytes);
  and and_9 (and_9_out, and_5_out, dreiBytes);
  assign controlled_buffer_8_out = and_5_out ? FrameBuffer_q : 8'bz;  // Controlled_Buffer controlled_buffer_8
  assign controlled_buffer_8_out = and_2_out ? register_2_q : 8'bz;  // Controlled_Buffer controlled_buffer_9
  assign controlled_buffer_8_out = and_3_out ? register_3_q : 8'bz;  // Controlled_Buffer controlled_buffer_10
  assign controlled_buffer_8_out = and_4_out ? register_4_q : 8'bz;  // Controlled_Buffer controlled_buffer_11
  Pull_Resistor pull_resistor_3 (.node(controlled_buffer_8_out));
  assign controlled_buffer_12_out = and_8_out ? FrameBuffer_q : 8'bz;  // Controlled_Buffer controlled_buffer_12
  assign controlled_buffer_12_out = and_9_out ? register_2_q : 8'bz;  // Controlled_Buffer controlled_buffer_13
  assign controlled_buffer_12_out = and_6_out ? register_3_q : 8'bz;  // Controlled_Buffer controlled_buffer_14
  assign controlled_buffer_12_out = and_7_out ? register_4_q : 8'bz;  // Controlled_Buffer controlled_buffer_15
  Pull_Resistor pull_resistor_4 (.node(controlled_buffer_12_out));
  Multiplexer #(.width(8)) multiplexer_1 (
    .in0(controlled_buffer_4_out), .in1(Opcode), .out(multiplexer_1_out), .sel(d_ff_2_q));
  or or_2 (or_2_out, and_7_out, and_4_out, comparator_4_eq);
  Register register_5 (.D(controlled_buffer_4_out), .en(d_ff_2_qn), .clk(CLK), .Q(Opcode));  // open: clr
  not not_2 (Valid, and_11_out);
  D_Flip_Flop d_ff_1 (.D(adder_2_cout), .clk(CLK), .Qn(d_ff_1_qn));  // open: Q, preset, reset
  not not_3 (not_3_out, adder_2_cout);
  and and_10 (and_10_out, not_3_out, or_2_out);
  D_Flip_Flop d_ff_2 (.D(and_11_out), .clk(CLK), .Q(d_ff_2_q), .Qn(d_ff_2_qn));  // open: preset, reset
  Register register_6 (.D(controlled_buffer_8_out), .en(zweiBytes), .clk(CLK), .Q(Operand1));  // open: clr
  Register register_7 (.D(controlled_buffer_12_out), .en(dreiBytes), .clk(CLK), .Q(Operand2));  // open: clr
  and and_11 (and_11_out, d_ff_1_qn, adder_2_cout);
  or or_3 (PC_Enable, and_11_out, and_10_out);

  // Other names for the same wires on the sheet: nextInstruction = Valid
endmodule

module MinimalOpcodeDecoder (
  input  [7:0] Instruction,
  output einByte,
  output zweiBytes,
  output dreiBytes
);

  wire not_1_out, not_2_out;

  // Probe on Instruction
  nor nor_1 (einByte, Instruction[7], Instruction[6]);
  not not_1 (not_1_out, Instruction[7]);
  and and_1 (zweiBytes, not_1_out, Instruction[6]);
  and and_2 (dreiBytes, Instruction[7], not_2_out);
  not not_2 (not_2_out, Instruction[6]);
endmodule

module InstLengthDecFast (
  input  [7:0] Byte_1,
  input  [7:0] Byte_2,
  input  [7:0] Byte_3,
  input  [7:0] Byte_4,
  input  PrevAck,
  input  PostAck,
  output [47:0] Instruction,
  output ReqPrev
);

  wire Acknowledged, and_1_out, and_2_out, and_3_out, and_4_out, and_5_out, and_6_out, and_7_out, and_8_out,
       and_9_out, and_10_out, and_11_out, buffer_1_out, buffer_2_out, buffer_3_out, buffer_4_out,
       buffer_5_out, buffer_6_out, buffer_7_out, buffer_8_out, buffer_9_out, buffer_10_out, buffer_11_out,
       buffer_12_out, buffer_13_out, buffer_14_out, buffer_15_out, buffer_16_out, buffer_17_out,
       buffer_18_out, buffer_19_out, buffer_20_out, buffer_21_out, buffer_22_out, buffer_23_out,
       buffer_24_out, buffer_25_out, buffer_26_out, buffer_27_out, buffer_28_out, buffer_29_out,
       buffer_30_out, buffer_31_out, buffer_32_out, buffer_33_out, buffer_34_out, buffer_35_out,
       buffer_36_out, buffer_37_out, buffer_38_out, buffer_39_out, buffer_40_out, buffer_41_out,
       buffer_42_out, buffer_43_out, buffer_44_out, buffer_45_out, buffer_46_out, buffer_47_out,
       buffer_48_out, buffer_49_out, buffer_50_out, buffer_51_out, buffer_52_out, buffer_53_out,
       buffer_54_out, buffer_55_out, buffer_56_out, Changed_q, comparator_1_eq, comparator_2_eq,
       comparator_3_eq, comparator_4_eq, dreiBytes, edgedetector_1_out_2, edgedetector_2_out_2, Inc,
       IncDelay, Leader_qn, LoadNext_q, LoadNext_qn, minimalopcodedecoder_1_einbyte,
       minimalopcodedecoder_1_zweibytes, NOP, nor_1_out, not_1_out, notEmpty, or_1_out, or_3_out, or_7_out,
       or_8_out, or_9_out, or_10_out, Overflow, posedgedetector_1_out_2, posedgedetector_2_out_2,
       posedgedetector_4_out_2, Request, RequestPermission, s_r_ff_1_q, Switch, xnor_1_out, xor_1_out,
       zweiBytes;
  wire [1:0] adder_1_out, controlled_buffer_1_out, FramesLoaded_q, register_1_q;
  wire [7:0] controlled_buffer_4_out, controlled_buffer_8_out, controlled_buffer_12_out,
       controlled_buffer_16_out, controlled_buffer_20_out, controlled_buffer_24_out, FrameBuffer1_q,
       FrameBuffer2_q, multiplexer_1_out, multiplexer_2_out, multiplexer_3_out, register_2_q, register_3_q,
       register_4_q, register_5_q, register_6_q, register_7_q;

  EdgeDetector edgedetector_1 (.in_1(PrevAck), .out_2(edgedetector_1_out_2));
  PosEdgeDetector posedgedetector_1 (.in_1(Switch), .out_2(posedgedetector_1_out_2));
  S_R_Flip_Flop Changed (.Q(Changed_q), .reset(and_1_out), .preset(edgedetector_1_out_2));  // open: S, R, clk, Qn
  buf buffer_1 (buffer_1_out, Changed_q);
  or or_1 (or_1_out, edgedetector_1_out_2, posedgedetector_1_out_2);
  buf buffer_2 (buffer_2_out, buffer_1_out);
  buf buffer_3 (buffer_3_out, buffer_2_out);
  Counter #(.max('h3), .width(2)) FramesLoaded (
    .up(edgedetector_1_out_2), .count(1'b1), .clk(or_1_out), .Q(FramesLoaded_q));  // open: clr, load, D, carry
  buf buffer_4 (buffer_4_out, buffer_3_out);
  buf buffer_5 (buffer_5_out, buffer_4_out);
  buf buffer_6 (buffer_6_out, buffer_5_out);
  buf buffer_7 (buffer_7_out, buffer_6_out);
  buf buffer_8 (buffer_8_out, buffer_7_out);
  and and_1 (and_1_out, buffer_8_out, RequestPermission);
  MinimalOpcodeDecoder minimalopcodedecoder_1 (
    .Instruction(multiplexer_1_out), .einByte(minimalopcodedecoder_1_einbyte),
    .zweiBytes(minimalopcodedecoder_1_zweibytes), .dreiBytes(dreiBytes));
  T_Flip_Flop LoadNext (.T(1'b1), .clk(edgedetector_1_out_2), .Q(LoadNext_q), .Qn(LoadNext_qn));  // open: reset, preset
  or or_2 (notEmpty, FramesLoaded_q[0], FramesLoaded_q[1]);
  and and_2 (and_2_out, FramesLoaded_q[0], FramesLoaded_q[1]);
  T_Flip_Flop t_ff_1 (.T(1'b1), .clk(and_1_out), .Qn(ReqPrev));  // open: Q, reset, preset
  and and_3 (and_3_out, IncDelay, NOP);
  assign controlled_buffer_1_out = minimalopcodedecoder_1_einbyte ? 2'b01 : 2'bz;  // Controlled_Buffer controlled_buffer_1
  assign controlled_buffer_1_out = minimalopcodedecoder_1_zweibytes ? 2'b10 : 2'bz;  // Controlled_Buffer controlled_buffer_2
  assign controlled_buffer_1_out = dreiBytes ? 2'b11 : 2'bz;  // Controlled_Buffer controlled_buffer_3
  Pull_Resistor pull_resistor_1 (.node(controlled_buffer_1_out));
  T_Flip_Flop Leader (.T(1'b1), .clk(Switch), .Qn(Leader_qn));  // open: Q, reset, preset
  nor nor_1 (nor_1_out, FramesLoaded_q[1], and_2_out);
  or or_3 (or_3_out, and_3_out, Acknowledged);
  buf buffer_9 (buffer_9_out, or_3_out);
  buf buffer_10 (buffer_10_out, buffer_9_out);
  Adder #(.width(2)) adder_1 (.a(register_1_q), .b(controlled_buffer_1_out), .out(adder_1_out));  // open: cin, cout
  buf buffer_11 (buffer_11_out, buffer_10_out);
  buf buffer_12 (buffer_12_out, buffer_11_out);
  Register #(.width(2)) register_1 (.D(adder_1_out), .en(1'b1), .clk(Inc), .Q(register_1_q));  // open: clr
  xnor xnor_1 (xnor_1_out, LoadNext_q, Leader_qn);
  buf buffer_13 (buffer_13_out, buffer_15_out);
  buf buffer_14 (buffer_14_out, buffer_12_out);
  buf buffer_15 (buffer_15_out, buffer_14_out);
  Register FrameBuffer1 (.D(Byte_1), .en(1'b1), .clk(LoadNext_q), .Q(FrameBuffer1_q));  // open: clr
  Register register_2 (.D(Byte_2), .en(1'b1), .clk(LoadNext_q), .Q(register_2_q));  // open: clr
  Register register_3 (.D(Byte_3), .en(1'b1), .clk(LoadNext_q), .Q(register_3_q));  // open: clr
  Register register_4 (.D(Byte_4), .en(1'b1), .clk(LoadNext_q), .Q(register_4_q));  // open: clr
  Register FrameBuffer2 (.D(Byte_1), .en(1'b1), .clk(LoadNext_qn), .Q(FrameBuffer2_q));  // open: clr
  Register register_5 (.D(Byte_2), .en(1'b1), .clk(LoadNext_qn), .Q(register_5_q));  // open: clr
  Register register_6 (.D(Byte_3), .en(1'b1), .clk(LoadNext_qn), .Q(register_6_q));  // open: clr
  Register register_7 (.D(Byte_4), .en(1'b1), .clk(LoadNext_qn), .Q(register_7_q));  // open: clr
  or or_4 (RequestPermission, xnor_1_out, nor_1_out);
  buf buffer_16 (buffer_16_out, buffer_13_out);
  buf buffer_17 (buffer_17_out, buffer_16_out);
  buf buffer_18 (buffer_18_out, buffer_17_out);
  Comparator #(.mode("unsigned"), .width(2)) comparator_1 (
    .a(2'b00), .b(register_1_q), .eq(comparator_1_eq));  // open: gt, lt
  Comparator #(.mode("unsigned"), .width(2)) comparator_2 (
    .a(2'b01), .b(register_1_q), .eq(comparator_2_eq));  // open: gt, lt
  Comparator #(.mode("unsigned"), .width(2)) comparator_3 (
    .a(2'b10), .b(register_1_q), .eq(comparator_3_eq));  // open: gt, lt
  Comparator #(.mode("unsigned"), .width(2)) comparator_4 (
    .a(2'b11), .b(register_1_q), .eq(comparator_4_eq));  // open: gt, lt
  buf buffer_19 (buffer_19_out, buffer_18_out);
  buf buffer_20 (buffer_20_out, buffer_19_out);
  or or_5 (zweiBytes, dreiBytes, minimalopcodedecoder_1_zweibytes);
  assign controlled_buffer_4_out = comparator_1_eq ? FrameBuffer1_q : 8'bz;  // Controlled_Buffer controlled_buffer_4
  assign controlled_buffer_4_out = comparator_2_eq ? register_2_q : 8'bz;  // Controlled_Buffer controlled_buffer_5
  assign controlled_buffer_4_out = comparator_3_eq ? register_3_q : 8'bz;  // Controlled_Buffer controlled_buffer_6
  assign controlled_buffer_4_out = comparator_4_eq ? register_4_q : 8'bz;  // Controlled_Buffer controlled_buffer_7
  assign controlled_buffer_8_out = comparator_1_eq ? FrameBuffer2_q : 8'bz;  // Controlled_Buffer controlled_buffer_8
  assign controlled_buffer_8_out = comparator_2_eq ? register_5_q : 8'bz;  // Controlled_Buffer controlled_buffer_9
  assign controlled_buffer_8_out = comparator_3_eq ? register_6_q : 8'bz;  // Controlled_Buffer controlled_buffer_10
  assign controlled_buffer_8_out = comparator_4_eq ? register_7_q : 8'bz;  // Controlled_Buffer controlled_buffer_11
  xor xor_1 (xor_1_out, Leader_qn, Overflow);
  buf buffer_21 (buffer_21_out, buffer_20_out);
  buf buffer_22 (buffer_22_out, buffer_21_out);
  buf buffer_23 (buffer_23_out, buffer_22_out);
  and and_4 (and_4_out, comparator_1_eq, zweiBytes);
  and and_5 (and_5_out, comparator_2_eq, zweiBytes);
  and and_6 (and_6_out, comparator_3_eq, zweiBytes);
  and and_7 (and_7_out, comparator_4_eq, zweiBytes);
  Multiplexer #(.width(8)) multiplexer_1 (
    .in0(controlled_buffer_8_out), .in1(controlled_buffer_4_out), .out(multiplexer_1_out), .sel(Leader_qn));
  Pull_Resistor pull_resistor_2 (.node(multiplexer_1_out));
  buf buffer_24 (buffer_24_out, buffer_23_out);
  and and_8 (and_8_out, and_4_out, dreiBytes);
  and and_9 (and_9_out, and_5_out, dreiBytes);
  and and_10 (and_10_out, and_6_out, dreiBytes);
  and and_11 (and_11_out, and_7_out, dreiBytes);
  assign controlled_buffer_12_out = and_7_out ? FrameBuffer1_q : 8'bz;  // Controlled_Buffer controlled_buffer_12
  assign controlled_buffer_12_out = and_4_out ? register_2_q : 8'bz;  // Controlled_Buffer controlled_buffer_13
  assign controlled_buffer_12_out = and_5_out ? register_3_q : 8'bz;  // Controlled_Buffer controlled_buffer_14
  assign controlled_buffer_12_out = and_6_out ? register_4_q : 8'bz;  // Controlled_Buffer controlled_buffer_15
  assign controlled_buffer_16_out = and_7_out ? FrameBuffer2_q : 8'bz;  // Controlled_Buffer controlled_buffer_16
  assign controlled_buffer_16_out = and_4_out ? register_5_q : 8'bz;  // Controlled_Buffer controlled_buffer_17
  assign controlled_buffer_16_out = and_5_out ? register_6_q : 8'bz;  // Controlled_Buffer controlled_buffer_18
  assign controlled_buffer_16_out = and_6_out ? register_7_q : 8'bz;  // Controlled_Buffer controlled_buffer_19
  Multiplexer #(.width(8)) multiplexer_2 (
    .in0(controlled_buffer_16_out), .in1(controlled_buffer_12_out), .out(multiplexer_2_out), .sel(xor_1_out));
  Pull_Resistor pull_resistor_3 (.node(multiplexer_2_out));
  PosEdgeDetector posedgedetector_2 (.in_1(notEmpty), .out_2(posedgedetector_2_out_2));
  S_R_Flip_Flop s_r_ff_1 (.Q(s_r_ff_1_q), .reset(IncDelay), .preset(posedgedetector_2_out_2));  // open: S, R, clk, Qn
  PosEdgeDetector posedgedetector_3 (.in_1(buffer_24_out), .out_2(Inc));
  or or_6 (Overflow, and_7_out, and_11_out, and_10_out);
  assign controlled_buffer_20_out = and_10_out ? FrameBuffer1_q : 8'bz;  // Controlled_Buffer controlled_buffer_20
  assign controlled_buffer_20_out = and_11_out ? register_2_q : 8'bz;  // Controlled_Buffer controlled_buffer_21
  assign controlled_buffer_20_out = and_8_out ? register_3_q : 8'bz;  // Controlled_Buffer controlled_buffer_22
  assign controlled_buffer_20_out = and_9_out ? register_4_q : 8'bz;  // Controlled_Buffer controlled_buffer_23
  assign controlled_buffer_24_out = and_10_out ? FrameBuffer2_q : 8'bz;  // Controlled_Buffer controlled_buffer_24
  assign controlled_buffer_24_out = and_11_out ? register_5_q : 8'bz;  // Controlled_Buffer controlled_buffer_25
  assign controlled_buffer_24_out = and_8_out ? register_6_q : 8'bz;  // Controlled_Buffer controlled_buffer_26
  assign controlled_buffer_24_out = and_9_out ? register_7_q : 8'bz;  // Controlled_Buffer controlled_buffer_27
  Multiplexer #(.width(8)) multiplexer_3 (
    .in0(controlled_buffer_24_out), .in1(controlled_buffer_20_out), .out(multiplexer_3_out), .sel(xor_1_out));
  Pull_Resistor pull_resistor_4 (.node(multiplexer_3_out));
  or or_7 (or_7_out, and_9_out, and_6_out, comparator_4_eq);
  or or_8 (or_8_out, and_9_out, and_6_out, comparator_4_eq);
  or or_9 (or_9_out, s_r_ff_1_q, Inc);
  buf buffer_25 (buffer_25_out, or_9_out);
  or or_10 (or_10_out, or_7_out, or_8_out);
  buf buffer_26 (buffer_26_out, buffer_25_out);
  buf buffer_27 (buffer_27_out, buffer_26_out);
  buf buffer_28 (buffer_28_out, buffer_27_out);
  and and_12 (Switch, or_10_out, Inc);
  Comparator #(.mode("unsigned")) comparator_5 (.a({8{1'b0}}), .b(multiplexer_1_out), .eq(NOP));  // open: gt, lt
  PosEdgeDetector posedgedetector_4 (.in_1(Request), .out_2(posedgedetector_4_out_2));
  buf buffer_29 (buffer_29_out, buffer_28_out);
  buf buffer_30 (buffer_30_out, buffer_29_out);
  buf buffer_31 (buffer_31_out, buffer_30_out);
  buf buffer_32 (buffer_32_out, buffer_31_out);
  buf buffer_33 (buffer_33_out, buffer_32_out);
  buf buffer_34 (buffer_34_out, buffer_33_out);
  buf buffer_35 (buffer_35_out, buffer_34_out);
  buf buffer_36 (buffer_36_out, buffer_35_out);
  not not_1 (not_1_out, NOP);
  and and_13 (Request, not_1_out, IncDelay);
  buf buffer_37 (buffer_37_out, buffer_36_out);
  buf buffer_38 (buffer_38_out, buffer_37_out);
  DRailByteSender drailbytesender_1 (
    .Acknowledge(PostAck), .Request(posedgedetector_4_out_2), .Byte(multiplexer_1_out),
    .DualRailByte(Instruction[47:32]));  // open: Fertig
  DRailByteSender drailbytesender_2 (
    .Acknowledge(PostAck), .Request(posedgedetector_4_out_2), .Byte(multiplexer_2_out),
    .DualRailByte(Instruction[31:16]));  // open: Fertig
  DRailByteSender drailbytesender_3 (
    .Acknowledge(PostAck), .Request(posedgedetector_4_out_2), .Byte(multiplexer_3_out),
    .DualRailByte(Instruction[15:0]));  // open: Fertig
  EdgeDetector edgedetector_2 (.in_1(PostAck), .out_2(edgedetector_2_out_2));
  buf buffer_39 (buffer_39_out, buffer_38_out);
  buf buffer_40 (buffer_40_out, buffer_39_out);
  buf buffer_41 (buffer_41_out, buffer_40_out);
  S_R_Flip_Flop s_r_ff_2 (.Q(Acknowledged), .reset(Inc), .preset(edgedetector_2_out_2));  // open: S, R, clk, Qn
  buf buffer_42 (buffer_42_out, buffer_41_out);
  buf buffer_43 (buffer_43_out, buffer_42_out);
  buf buffer_44 (buffer_44_out, buffer_43_out);
  buf buffer_45 (buffer_45_out, buffer_44_out);
  buf buffer_46 (buffer_46_out, buffer_45_out);
  buf buffer_47 (buffer_47_out, buffer_46_out);
  buf buffer_48 (buffer_48_out, buffer_47_out);
  buf buffer_49 (buffer_49_out, buffer_48_out);
  buf buffer_50 (buffer_50_out, buffer_49_out);
  buf buffer_51 (buffer_51_out, buffer_50_out);
  buf buffer_52 (buffer_52_out, buffer_51_out);
  buf buffer_53 (buffer_53_out, buffer_52_out);
  buf buffer_54 (buffer_54_out, buffer_53_out);
  buf buffer_55 (buffer_55_out, buffer_54_out);
  buf buffer_56 (buffer_56_out, buffer_55_out);
  and and_14 (IncDelay, buffer_56_out, notEmpty);
endmodule

module DRailBitSenderFull (
  input  Acknowledge,
  input  Request,
  input  Bit,
  output Fertig,
  output [1:0] DualRailBit
);

  wire edgedetector_1_out_2, edgedetector_2_out_2, not_1_out, posedgedetector_1_out_2, s_r_ff_1_q;

  EdgeDetector edgedetector_1 (.in_1(Request), .out_2(edgedetector_1_out_2));
  S_R_Flip_Flop s_r_ff_1 (
    .Q(s_r_ff_1_q), .reset(edgedetector_2_out_2), .preset(edgedetector_1_out_2));  // open: S, R, clk, Qn
  EdgeDetector edgedetector_2 (.in_1(Acknowledge), .out_2(edgedetector_2_out_2));
  S_R_Flip_Flop Empfangen (
    .Q(Fertig), .reset(posedgedetector_1_out_2), .preset(edgedetector_2_out_2));  // open: S, R, clk, Qn
  PosEdgeDetector posedgedetector_1 (.in_1(s_r_ff_1_q), .out_2(posedgedetector_1_out_2));
  T_Flip_Flop t_ff_1 (.T(not_1_out), .clk(posedgedetector_1_out_2), .Q(DualRailBit[0]));  // open: Qn, reset, preset
  not not_1 (not_1_out, Bit);
  T_Flip_Flop t_ff_2 (.T(Bit), .clk(posedgedetector_1_out_2), .Q(DualRailBit[1]));  // open: Qn, reset, preset
endmodule
