// Logisim project Asynchronous3.circ as structural Verilog: 29 circuits, main circuit main
module main (
  input  [1:0] A,
  input  [1:0] B,
  output [1:0] C
);

  wire and_1_out, and_2_out, and_3_out, and_4_out, and_5_out, and_6_out, and_7_out, and_8_out, c_element_1_c,
       c_element_2_c, c_element_3_c, not_1_out, not_2_out, not_3_out, not_4_out, or_1_out, or_2_out,
       or_3_out, or_4_out, xor_1_out;

  not not_1 (not_1_out, xor_1_out);
  not not_2 (not_2_out, xor_1_out);
  not not_3 (not_3_out, xor_1_out);
  not not_4 (not_4_out, xor_1_out);
  and and_1 (and_1_out, A[0], not_1_out);
  or or_1 (or_1_out, and_1_out, and_2_out);
  and and_2 (and_2_out, A[0], xor_1_out);
  and and_3 (and_3_out, A[1], not_2_out);
  or or_2 (or_2_out, and_3_out, and_4_out);
  and and_4 (and_4_out, A[1], xor_1_out);
  and and_5 (and_5_out, B[0], not_3_out);
  or or_3 (or_3_out, and_5_out, and_6_out);
  and and_6 (and_6_out, B[0], xor_1_out);
  and and_7 (and_7_out, B[1], not_4_out);
  or or_4 (or_4_out, and_7_out, and_8_out);
  and and_8 (and_8_out, B[1], xor_1_out);
  C_Element c_element_1 (.A(or_1_out), .B(or_3_out), .C(c_element_1_c));
  C_Element c_element_2 (.A(or_1_out), .B(or_4_out), .C(c_element_2_c));
  C_Element c_element_3 (.A(or_2_out), .B(or_3_out), .C(c_element_3_c));
  C_Element c_element_4 (.A(or_2_out), .B(or_4_out), .C(C[1]));
  or or_5 (C[0], c_element_1_c, c_element_2_c, c_element_3_c);
  xor xor_1 (xor_1_out, C[1], C[0]);
endmodule

module C_Element (
  input  A,
  input  B,
  output C
);

  wire and_1_out, nor_1_out;

  and and_1 (and_1_out, A, B);
  S_R_Flip_Flop s_r_ff_1 (.S(1'b0), .R(1'b0), .clk(1'b0), .Q(C), .reset(nor_1_out), .preset(and_1_out));  // open: Qn
  nor nor_1 (nor_1_out, A, B);
endmodule

module Muller_Pipeline (
  input  Acknowledge2,
  input  Request,
  output Acknowledge,
  output Request2
);

  wire c_element_2_c, c_element_3_c, not_1_out, not_2_out, not_3_out, not_4_out;

  not not_1 (not_1_out, c_element_2_c);
  C_Element c_element_1 (.A(not_1_out), .B(Request), .C(Acknowledge));
  not not_2 (not_2_out, c_element_3_c);
  C_Element c_element_2 (.A(not_2_out), .B(Acknowledge), .C(c_element_2_c));
  not not_3 (not_3_out, Request2);
  C_Element c_element_3 (.A(not_3_out), .B(c_element_2_c), .C(c_element_3_c));
  not not_4 (not_4_out, Acknowledge2);
  C_Element c_element_4 (.A(not_4_out), .B(c_element_3_c), .C(Request2));
endmodule

module FourP_Latch (
  input  [7:0] Data_In,
  input  EN,
  output [7:0] Data_Out
);

  Register register_1 (.D(Data_In), .en(1'b1), .clk(EN), .Q(Data_Out));  // open: clr
endmodule

module FourP_BundD_Pipeline (
  input  Acknowledge2,
  input  Request,
  input  [7:0] Data,
  output Acknowledge,
  output Request2,
  output [7:0] Data2
);

  wire buffer_1_out, buffer_2_out, buffer_3_out, buffer_4_out, buffer_5_out, buffer_6_out, buffer_7_out,
       buffer_8_out, buffer_9_out, buffer_10_out, buffer_11_out, buffer_12_out, fourp_storageelement_1_ro,
       fourp_storageelement_2_ai, fourp_storageelement_2_ro, fourp_storageelement_3_ai,
       fourp_storageelement_3_ro, fourp_storageelement_4_ai;
  wire [7:0] adder_1_out, fourp_storageelement_1_data_out, fourp_storageelement_2_data_out,
       fourp_storageelement_3_data_out;

  FourP_StorageElement fourp_storageelement_1 (
    .Ri(Request), .Data_In(Data), .Ao(fourp_storageelement_2_ai), .Ai(Acknowledge),
    .Data_Out(fourp_storageelement_1_data_out), .Ro(fourp_storageelement_1_ro));
  buf buffer_1 (buffer_1_out, fourp_storageelement_1_ro);
  buf buffer_2 (buffer_2_out, buffer_1_out);
  buf buffer_3 (buffer_3_out, buffer_2_out);
  buf buffer_4 (buffer_4_out, buffer_3_out);
  buf buffer_5 (buffer_5_out, buffer_4_out);
  Adder adder_1 (.a(fourp_storageelement_1_data_out), .b(8'h3), .out(adder_1_out));  // open: cin, cout
  buf buffer_6 (buffer_6_out, buffer_5_out);
  buf buffer_7 (buffer_7_out, buffer_6_out);
  buf buffer_8 (buffer_8_out, buffer_7_out);
  buf buffer_9 (buffer_9_out, buffer_8_out);
  buf buffer_10 (buffer_10_out, buffer_9_out);
  buf buffer_11 (buffer_11_out, buffer_10_out);
  buf buffer_12 (buffer_12_out, buffer_11_out);
  FourP_StorageElement fourp_storageelement_2 (
    .Ri(buffer_12_out), .Data_In(adder_1_out), .Ao(fourp_storageelement_3_ai),
    .Ai(fourp_storageelement_2_ai), .Data_Out(fourp_storageelement_2_data_out), .Ro(fourp_storageelement_2_ro));
  FourP_StorageElement fourp_storageelement_3 (
    .Ri(fourp_storageelement_2_ro), .Data_In(fourp_storageelement_2_data_out),
    .Ao(fourp_storageelement_4_ai), .Ai(fourp_storageelement_3_ai),
    .Data_Out(fourp_storageelement_3_data_out), .Ro(fourp_storageelement_3_ro));
  FourP_StorageElement fourp_storageelement_4 (
    .Ri(fourp_storageelement_3_ro), .Data_In(fourp_storageelement_3_data_out), .Ao(Acknowledge2),
    .Ai(fourp_storageelement_4_ai), .Data_Out(Data2), .Ro(Request2));
endmodule

module FourP_StorageElement (
  input  Ao,
  input  Ri,
  input  [7:0] Data_In,
  output Ai,
  output Ro,
  output [7:0] Data_Out
);

  wire buffer_1_out, not_1_out;

  C_Element c_element_1 (.A(not_1_out), .B(Ri), .C(Ai));
  not not_1 (not_1_out, Ao);
  FourP_Latch fourp_latch_1 (.Data_In(Data_In), .EN(Ai), .Data_Out(Data_Out));
  buf buffer_1 (buffer_1_out, Ai);
  buf buffer_2 (Ro, buffer_1_out);
endmodule

module CP_Latch (
  input  [7:0] Data_In,
  input  C,
  input  P,
  output [7:0] Data_Out
);

  wire not_1_out;
  wire [7:0] register_1_q, register_2_q;

  Register register_1 (.D(Data_In), .en(1'b1), .clk(C), .Q(register_1_q));  // open: clr
  Register register_2 (.D(Data_In), .en(1'b1), .clk(not_1_out), .Q(register_2_q));  // open: clr
  not not_1 (not_1_out, C);
  Multiplexer #(.width(8)) multiplexer_1 (.in0(register_1_q), .in1(register_2_q), .out(Data_Out), .sel(P));
endmodule

module TwoP_BundD_Pipeline (
  input  Acknowledge2,
  input  Request,
  input  [7:0] Data,
  output Acknowledge,
  output Request2,
  output [7:0] Data2
);

  wire buffer_1_out, buffer_2_out, buffer_3_out, buffer_4_out, buffer_5_out, buffer_6_out, buffer_7_out,
       buffer_8_out, buffer_9_out, buffer_10_out, buffer_11_out, buffer_12_out, twop_storageelement_1_ro,
       twop_storageelement_2_ai, twop_storageelement_2_ro, twop_storageelement_3_ai,
       twop_storageelement_3_ro, twop_storageelement_4_ai;
  wire [7:0] adder_1_out, twop_storageelement_1_data_out, twop_storageelement_2_data_out,
       twop_storageelement_3_data_out;

  TwoP_StorageElement twop_storageelement_1 (
    .Ri(Request), .Data_In(Data), .Ao(twop_storageelement_2_ai), .Ai(Acknowledge),
    .Data_Out(twop_storageelement_1_data_out), .Ro(twop_storageelement_1_ro));
  buf buffer_1 (buffer_1_out, twop_storageelement_1_ro);
  buf buffer_2 (buffer_2_out, buffer_1_out);
  buf buffer_3 (buffer_3_out, buffer_2_out);
  buf buffer_4 (buffer_4_out, buffer_3_out);
  buf buffer_5 (buffer_5_out, buffer_4_out);
  Adder adder_1 (.a(twop_storageelement_1_data_out), .b(8'h3), .out(adder_1_out));  // open: cin, cout
  buf buffer_6 (buffer_6_out, buffer_5_out);
  buf buffer_7 (buffer_7_out, buffer_6_out);
  buf buffer_8 (buffer_8_out, buffer_7_out);
  buf buffer_9 (buffer_9_out, buffer_8_out);
  buf buffer_10 (buffer_10_out, buffer_9_out);
  buf buffer_11 (buffer_11_out, buffer_10_out);
  buf buffer_12 (buffer_12_out, buffer_11_out);
  TwoP_StorageElement twop_storageelement_2 (
    .Ri(buffer_12_out), .Data_In(adder_1_out), .Ao(twop_storageelement_3_ai), .Ai(twop_storageelement_2_ai),
    .Data_Out(twop_storageelement_2_data_out), .Ro(twop_storageelement_2_ro));
  TwoP_StorageElement twop_storageelement_3 (
    .Ri(twop_storageelement_2_ro), .Data_In(twop_storageelement_2_data_out), .Ao(twop_storageelement_4_ai),
    .Ai(twop_storageelement_3_ai), .Data_Out(twop_storageelement_3_data_out), .Ro(twop_storageelement_3_ro));
  TwoP_StorageElement twop_storageelement_4 (
    .Ri(twop_storageelement_3_ro), .Data_In(twop_storageelement_3_data_out), .Ao(Acknowledge2),
    .Ai(twop_storageelement_4_ai), .Data_Out(Data2), .Ro(Request2));
endmodule

module TwoP_StorageElement (
  input  Ao,
  input  Ri,
  input  [7:0] Data_In,
  output Ai,
  output Ro,
  output [7:0] Data_Out
);

  wire buffer_1_out, buffer_2_out, buffer_3_out, buffer_4_out, buffer_5_out, not_1_out;

  not not_1 (not_1_out, Ao);
  C_Element c_element_1 (.A(not_1_out), .B(Ri), .C(Ai));
  CP_Latch cp_latch_1 (.Data_In(Data_In), .C(Ai), .P(Ao), .Data_Out(Data_Out));
  buf buffer_1 (buffer_1_out, Ai);
  buf buffer_2 (buffer_2_out, buffer_1_out);
  buf buffer_3 (buffer_3_out, buffer_2_out);
  buf buffer_4 (buffer_4_out, buffer_3_out);
  buf buffer_5 (buffer_5_out, buffer_4_out);
  buf buffer_6 (Ro, buffer_5_out);
endmodule

module ByteDRail_Latch (
  input  Ao,
  input  [15:0] Rails_In,
  output Ai,
  output [15:0] Rails_Out
);

  wire and_1_out, nor_1_out, not_1_out, or_1_out, or_2_out, or_3_out, or_4_out, or_5_out, or_6_out, or_7_out,
       or_8_out;

  not not_1 (not_1_out, Ao);
  C_Element c_element_1 (.A(not_1_out), .B(Rails_In[0]), .C(Rails_Out[0]));
  C_Element c_element_2 (.A(not_1_out), .B(Rails_In[1]), .C(Rails_Out[1]));
  C_Element c_element_3 (.A(not_1_out), .B(Rails_In[2]), .C(Rails_Out[2]));
  C_Element c_element_4 (.A(not_1_out), .B(Rails_In[3]), .C(Rails_Out[3]));
  C_Element c_element_5 (.A(not_1_out), .B(Rails_In[4]), .C(Rails_Out[4]));
  C_Element c_element_6 (.A(not_1_out), .B(Rails_In[5]), .C(Rails_Out[5]));
  C_Element c_element_7 (.A(not_1_out), .B(Rails_In[6]), .C(Rails_Out[6]));
  C_Element c_element_8 (.A(not_1_out), .B(Rails_In[7]), .C(Rails_Out[7]));
  C_Element c_element_9 (.A(not_1_out), .B(Rails_In[8]), .C(Rails_Out[8]));
  C_Element c_element_10 (.A(not_1_out), .B(Rails_In[9]), .C(Rails_Out[9]));
  C_Element c_element_11 (.A(not_1_out), .B(Rails_In[10]), .C(Rails_Out[10]));
  C_Element c_element_12 (.A(not_1_out), .B(Rails_In[11]), .C(Rails_Out[11]));
  C_Element c_element_13 (.A(not_1_out), .B(Rails_In[12]), .C(Rails_Out[12]));
  C_Element c_element_14 (.A(not_1_out), .B(Rails_In[13]), .C(Rails_Out[13]));
  C_Element c_element_15 (.A(not_1_out), .B(Rails_In[14]), .C(Rails_Out[14]));
  C_Element c_element_16 (.A(not_1_out), .B(Rails_In[15]), .C(Rails_Out[15]));
  and and_1 (and_1_out, or_1_out, or_2_out, or_4_out, or_3_out, or_5_out, or_6_out, or_7_out, or_8_out);
  or or_1 (or_1_out, Rails_Out[0], Rails_Out[1]);
  or or_2 (or_2_out, Rails_Out[2], Rails_Out[3]);
  C_Element c_element_17 (.A(and_1_out), .B(nor_1_out), .C(Ai));
  nor nor_1 (nor_1_out, or_1_out, or_2_out, or_4_out, or_3_out, or_5_out, or_6_out, or_7_out, or_8_out);
  or or_3 (or_3_out, Rails_Out[6], Rails_Out[7]);
  or or_4 (or_4_out, Rails_Out[4], Rails_Out[5]);
  or or_5 (or_5_out, Rails_Out[8], Rails_Out[9]);
  or or_6 (or_6_out, Rails_Out[10], Rails_Out[11]);
  or or_7 (or_7_out, Rails_Out[12], Rails_Out[13]);
  or or_8 (or_8_out, Rails_Out[14], Rails_Out[15]);
endmodule

module TwoP_DRail_Pipeline (
  input  in_1,
  input  [15:0] in_2,
  output out_3,
  output [15:0] out_4
);

  wire bytedrail_latch_3_ai, bytedrail_latch_4_ai;
  wire [15:0] bytedrail_latch_2_rails_out, bytedrail_latch_3_rails_out;

  ByteDRail_Latch bytedrail_latch_1 (.Ao(in_1), .Rails_In(in_2), .Rails_Out(out_4), .Ai(out_3));
  ByteDRail_Latch bytedrail_latch_2 (
    .Ao(bytedrail_latch_3_ai), .Rails_Out(bytedrail_latch_2_rails_out));  // open: Rails_In, Ai
  ByteDRail_Latch bytedrail_latch_3 (
    .Ao(bytedrail_latch_4_ai), .Rails_In(bytedrail_latch_2_rails_out),
    .Rails_Out(bytedrail_latch_3_rails_out), .Ai(bytedrail_latch_3_ai));
  ByteDRail_Latch bytedrail_latch_4 (
    .Rails_In(bytedrail_latch_3_rails_out), .Ai(bytedrail_latch_4_ai));  // open: Ao, Rails_Out
endmodule

module FourP_DRail_And (
  input  [1:0] A,
  input  [1:0] B,
  output [1:0] C
);

  wire c_element_1_c, c_element_2_c, c_element_3_c;

  C_Element c_element_1 (.A(A[0]), .B(B[0]), .C(c_element_1_c));
  C_Element c_element_2 (.A(A[0]), .B(B[1]), .C(c_element_2_c));
  C_Element c_element_3 (.A(A[1]), .B(B[0]), .C(c_element_3_c));
  C_Element c_element_4 (.A(A[1]), .B(B[1]), .C(C[1]));
  or or_1 (C[0], c_element_1_c, c_element_2_c, c_element_3_c);
endmodule

module FourP_DRail_BitMerge (
  input  CAck,
  input  [1:0] A,
  input  [1:0] B,
  output AAck,
  output [1:0] C,
  output BAck
);

  wire or_1_out, or_2_out;

  C_Element c_element_1 (.A(or_1_out), .B(CAck), .C(AAck));
  C_Element c_element_2 (.A(CAck), .B(or_2_out), .C(BAck));
  or or_1 (or_1_out, A[0], A[1]);
  or or_2 (or_2_out, B[0], B[1]);
  or or_3 (C[1], A[1], B[1]);
  or or_4 (C[0], A[0], B[0]);
endmodule

module FourP_MUTEX (
  input  Ri1,
  input  Ri2,
  output Ro1,
  output Ro2
);

  wire not_1_out, not_2_out;

  C_Element c_element_1 (.A(Ri1), .B(not_1_out), .C(Ro1));
  not not_1 (not_1_out, Ri2);
  not not_2 (not_2_out, Ro1);
  C_Element c_element_2 (.A(not_2_out), .B(Ri2), .C(Ro2));
endmodule

module TwoP_MUTEX (
  input  Ri1,
  input  Ao1,
  input  Ri2,
  input  Ao2,
  output Ro1,
  output Ro2
);

  wire and_1_out, and_2_out, and_3_out, c_element_1_c, c_element_2_c, edgedetector_1_out_2,
       edgedetector_2_out_2, edgedetector_3_out_2, edgedetector_4_out_2, not_1_out, not_2_out, not_3_out,
       s_r_ff_1_q, s_r_ff_2_q;

  EdgeDetector edgedetector_1 (.in_1(Ri1), .out_2(edgedetector_1_out_2));
  S_R_Flip_Flop s_r_ff_1 (
    .Q(s_r_ff_1_q), .reset(edgedetector_2_out_2), .preset(edgedetector_1_out_2));  // open: S, R, clk, Qn
  EdgeDetector edgedetector_2 (.in_1(Ao1), .out_2(edgedetector_2_out_2));
  EdgeDetector edgedetector_3 (.in_1(Ri2), .out_2(edgedetector_3_out_2));
  S_R_Flip_Flop s_r_ff_2 (
    .Q(s_r_ff_2_q), .reset(edgedetector_4_out_2), .preset(edgedetector_3_out_2));  // open: S, R, clk, Qn
  EdgeDetector edgedetector_4 (.in_1(Ao2), .out_2(edgedetector_4_out_2));
  C_Element c_element_1 (.A(s_r_ff_2_q), .B(not_1_out), .C(c_element_1_c));
  not not_1 (not_1_out, s_r_ff_1_q);
  and and_1 (and_1_out, s_r_ff_2_q, c_element_1_c);
  not not_2 (not_2_out, c_element_1_c);
  C_Element c_element_2 (.A(not_2_out), .B(s_r_ff_1_q), .C(c_element_2_c));
  not not_3 (not_3_out, c_element_2_c);
  and and_2 (and_2_out, c_element_2_c, s_r_ff_1_q);
  and and_3 (and_3_out, not_3_out, and_1_out);
  T_Flip_Flop t_ff_1 (.T(1'b1), .clk(and_2_out), .Q(Ro1));  // open: Qn, reset, preset
  T_Flip_Flop t_ff_2 (.T(1'b1), .clk(and_3_out), .Q(Ro2));  // open: Qn, reset, preset
endmodule

module TwoP_DRailBit_MUTEX_Merge (
  input  CAck,
  input  [1:0] A,
  input  [1:0] B,
  output AAck,
  output [1:0] C,
  output BAck
);

  wire drailbitcomparator_1_changed, drailbitcomparator_2_changed, drailbitcomparator_3_changed,
       edgedetector_1_out_2, edgedetector_2_out_2, edgedetector_3_out_2, edgedetector_4_out_2,
       edgedetector_5_out_2, edgedetector_6_out_2, s_r_ff_1_q, twop_mutex_1_ro1, twop_mutex_1_ro2;
  wire [1:0] multiplexer_1_out;

  EdgeDetector edgedetector_1 (.in_1(AAck), .out_2(edgedetector_1_out_2));
  EdgeDetector edgedetector_2 (.in_1(BAck), .out_2(edgedetector_2_out_2));
  T_Flip_Flop t_ff_1 (.T(twop_mutex_1_ro1), .clk(edgedetector_3_out_2), .Q(AAck));  // open: Qn, reset, preset
  T_Flip_Flop t_ff_2 (.T(twop_mutex_1_ro2), .clk(edgedetector_3_out_2), .Q(BAck));  // open: Qn, reset, preset
  DRailBitComparator drailbitcomparator_1 (
    .Remember(edgedetector_1_out_2), .Bit(A), .Changed(drailbitcomparator_1_changed));
  DRailBitComparator drailbitcomparator_2 (
    .Remember(edgedetector_2_out_2), .Bit(B), .Changed(drailbitcomparator_2_changed));
  TwoP_MUTEX twop_mutex_1 (
    .Ri1(drailbitcomparator_1_changed), .Ao1(AAck), .Ri2(drailbitcomparator_2_changed), .Ao2(BAck),
    .Ro1(twop_mutex_1_ro1), .Ro2(twop_mutex_1_ro2));
  S_R_Flip_Flop s_r_ff_1 (
    .Q(s_r_ff_1_q), .reset(edgedetector_4_out_2), .preset(edgedetector_5_out_2));  // open: S, R, clk, Qn
  Multiplexer #(.width(2)) multiplexer_1 (.in0(A), .in1(B), .out(multiplexer_1_out), .sel(s_r_ff_1_q));
  T_Flip_Flop t_ff_3 (.T(multiplexer_1_out[0]), .clk(edgedetector_6_out_2), .Q(C[0]));  // open: Qn, reset, preset
  T_Flip_Flop t_ff_4 (.T(multiplexer_1_out[1]), .clk(edgedetector_6_out_2), .Q(C[1]));  // open: Qn, reset, preset
  EdgeDetector edgedetector_3 (.in_1(CAck), .out_2(edgedetector_3_out_2));
  EdgeDetector edgedetector_4 (.in_1(twop_mutex_1_ro1), .out_2(edgedetector_4_out_2));
  EdgeDetector edgedetector_5 (.in_1(twop_mutex_1_ro2), .out_2(edgedetector_5_out_2));
  DRailBitComparator drailbitcomparator_3 (
    .Remember(edgedetector_3_out_2), .Bit(multiplexer_1_out), .Changed(drailbitcomparator_3_changed));
  EdgeDetector edgedetector_6 (.in_1(drailbitcomparator_3_changed), .out_2(edgedetector_6_out_2));
endmodule

module BitDRail_Latch (
  input  Ao,
  input  [1:0] Rails_In,
  output Ai,
  output Request,
  output [1:0] Rails_Out
);

  wire and_1_out, and_2_out, and_3_out, and_4_out, and_5_out, and_6_out, and_7_out, and_8_out, and_9_out,
       buffer_2_out, buffer_3_out, buffer_4_out, c_element_1_c, not_1_out, not_2_out, not_3_out, not_4_out,
       not_5_out, not_6_out, not_7_out, not_8_out, not_9_out, xor_1_out, xor_2_out, xor_3_out;

  not not_1 (not_1_out, Ao);
  and and_1 (and_1_out, not_1_out, Request);
  and and_2 (and_2_out, Request, Ao);
  not not_2 (not_2_out, c_element_1_c);
  and and_3 (and_3_out, not_2_out, and_1_out);
  C_Element c_element_1 (.A(and_3_out), .B(not_3_out), .C(c_element_1_c));
  not not_3 (not_3_out, and_2_out);
  buf buffer_1 (Ai, buffer_2_out);
  buf buffer_2 (buffer_2_out, buffer_3_out);
  xor xor_1 (xor_1_out, Ai, c_element_1_c);
  buf buffer_3 (buffer_3_out, buffer_4_out);
  buf buffer_4 (buffer_4_out, c_element_1_c);
  not not_4 (not_4_out, Rails_In[0]);
  not not_5 (not_5_out, Rails_In[1]);
  and and_4 (and_4_out, xor_1_out, Rails_In[0]);
  and and_5 (and_5_out, not_4_out, xor_1_out);
  and and_6 (and_6_out, xor_1_out, Rails_In[1]);
  and and_7 (and_7_out, not_5_out, xor_1_out);
  xor xor_2 (xor_2_out, Rails_In[0], Rails_Out[0]);
  not not_6 (not_6_out, Rails_Out[0]);
  and and_8 (and_8_out, not_6_out, and_4_out);
  C_Element c_element_2 (.A(and_8_out), .B(not_7_out), .C(Rails_Out[0]));
  not not_7 (not_7_out, and_5_out);
  xor xor_3 (xor_3_out, Rails_In[1], Rails_Out[1]);
  not not_8 (not_8_out, Rails_Out[1]);
  and and_9 (and_9_out, not_8_out, and_6_out);
  C_Element c_element_3 (.A(and_9_out), .B(not_9_out), .C(Rails_Out[1]));
  not not_9 (not_9_out, and_7_out);
  or or_1 (Request, xor_2_out, xor_3_out);
endmodule

module DRailBitComparator (
  input  Remember,
  input  [1:0] Bit,
  output Changed
);

  wire d_ff_1_q, d_ff_2_q, edgedetector_1_out_2, or_1_out, xor_1_out, xor_2_out;

  EdgeDetector edgedetector_1 (.in_1(Remember), .out_2(edgedetector_1_out_2));
  D_Flip_Flop d_ff_1 (.D(Bit[0]), .clk(edgedetector_1_out_2), .Q(d_ff_1_q));  // open: Qn, preset, reset
  D_Flip_Flop d_ff_2 (.D(Bit[1]), .clk(edgedetector_1_out_2), .Q(d_ff_2_q));  // open: Qn, preset, reset
  xor xor_1 (xor_1_out, Bit[0], d_ff_1_q);
  xor xor_2 (xor_2_out, Bit[1], d_ff_2_q);
  T_Flip_Flop t_ff_1 (.T(1'b1), .clk(or_1_out), .Q(Changed));  // open: Qn, reset, preset
  or or_1 (or_1_out, xor_1_out, xor_2_out);
endmodule

module TestBench (
  input  Request,
  input  Acknowledge2,
  input  [7:0] Data,
  output Acknowledge,
  output Request2,
  output [7:0] Data2
);

  wire buffer_1_out, buffer_2_out, buffer_3_out, buffer_4_out, buffer_5_out, buffer_6_out, buffer_7_out,
       buffer_8_out, buffer_9_out, buffer_10_out, buffer_11_out, buffer_12_out, fourp_arbiter_1_a1,
       fourp_arbiter_1_r0, twop_storageelement_1_ro, twop_storageelement_2_ai, twop_storageelement_2_ro,
       twop_storageelement_3_ai, twop_storageelement_3_ro, twop_storageelement_4_ai;
  wire [7:0] adder_1_out, twop_storageelement_1_data_out, twop_storageelement_3_data_out;

  TwoP_StorageElement twop_storageelement_1 (
    .Ri(Request), .Data_In(Data), .Ao(twop_storageelement_2_ai), .Ai(Acknowledge),
    .Data_Out(twop_storageelement_1_data_out), .Ro(twop_storageelement_1_ro));
  buf buffer_1 (buffer_1_out, twop_storageelement_1_ro);
  buf buffer_2 (buffer_2_out, buffer_1_out);
  buf buffer_3 (buffer_3_out, buffer_2_out);
  buf buffer_4 (buffer_4_out, buffer_3_out);
  buf buffer_5 (buffer_5_out, buffer_4_out);
  Adder adder_1 (.a(twop_storageelement_1_data_out), .b(8'h3), .out(adder_1_out));  // open: cin, cout
  buf buffer_6 (buffer_6_out, buffer_5_out);
  buf buffer_7 (buffer_7_out, buffer_6_out);
  buf buffer_8 (buffer_8_out, buffer_7_out);
  buf buffer_9 (buffer_9_out, buffer_8_out);
  buf buffer_10 (buffer_10_out, buffer_9_out);
  buf buffer_11 (buffer_11_out, buffer_10_out);
  buf buffer_12 (buffer_12_out, buffer_11_out);
  TwoP_StorageElement twop_storageelement_2 (
    .Ri(buffer_12_out), .Data_In(adder_1_out), .Ao(fourp_arbiter_1_a1), .Ai(twop_storageelement_2_ai),
    .Ro(twop_storageelement_2_ro));  // open: Data_Out
  FourP_Arbiter fourp_arbiter_1 (
    .A0(twop_storageelement_3_ai), .R1(twop_storageelement_2_ro), .R0(fourp_arbiter_1_r0),
    .A1(fourp_arbiter_1_a1));  // open: R2, A2
  TwoP_StorageElement twop_storageelement_3 (
    .Ri(fourp_arbiter_1_r0), .Ao(twop_storageelement_4_ai), .Ai(twop_storageelement_3_ai),
    .Data_Out(twop_storageelement_3_data_out), .Ro(twop_storageelement_3_ro));  // open: Data_In
  TwoP_StorageElement twop_storageelement_4 (
    .Ri(twop_storageelement_3_ro), .Data_In(twop_storageelement_3_data_out), .Ao(Acknowledge2),
    .Ai(twop_storageelement_4_ai), .Data_Out(Data2), .Ro(Request2));
endmodule

module FourP_Arbiter (
  input  R1,
  input  R2,
  input  A0,
  output A1,
  output R0,
  output A2
);

  wire and_1_out, and_2_out, fourp_mutex_1_ro1, fourp_mutex_1_ro2, not_1_out, not_2_out;

  FourP_MUTEX fourp_mutex_1 (.Ri1(R1), .Ri2(R2), .Ro1(fourp_mutex_1_ro1), .Ro2(fourp_mutex_1_ro2));
  not not_1 (not_1_out, A2);
  not not_2 (not_2_out, A1);
  C_Element c_element_1 (.A(and_1_out), .B(A0), .C(A1));
  and and_1 (and_1_out, not_1_out, fourp_mutex_1_ro1);
  and and_2 (and_2_out, fourp_mutex_1_ro2, not_2_out);
  C_Element c_element_2 (.A(A0), .B(and_2_out), .C(A2));
  or or_1 (R0, and_1_out, and_2_out);
endmodule

module FourP_BundD_MUX (
  input  CAck,
  input  AReq,
  input  BReq,
  input  A,
  input  B,
  input  [1:0] Ctl,
  output AAck,
  output CReq,
  output BAck,
  output C,
  output CtlAck
);

  wire c_element_1_c, c_element_2_c;

  C_Element c_element_1 (.A(AReq), .B(Ctl[0]), .C(c_element_1_c));
  C_Element c_element_2 (.A(BReq), .B(Ctl[1]), .C(c_element_2_c));
  C_Element c_element_3 (.A(c_element_1_c), .B(CAck), .C(AAck));
  C_Element c_element_4 (.A(c_element_2_c), .B(CAck), .C(BAck));
  or or_1 (CReq, c_element_1_c, c_element_2_c);
  Multiplexer multiplexer_1 (.in0(A), .in1(B), .out(C), .sel(Ctl[1]));

  assign CtlAck = CAck;
endmodule

module FourP_BundD_DEMUX (
  input  BAck,
  input  CAck,
  input  AReq,
  input  A,
  input  [1:0] Ctl,
  output AAck,
  output BReq,
  output CReq,
  output B,
  output C,
  output CtlAck
);

  C_Element c_element_1 (.A(AReq), .B(Ctl[0]), .C(BReq));
  C_Element c_element_2 (.A(AReq), .B(Ctl[1]), .C(CReq));
  or or_1 (AAck, BAck, CAck);

  assign B = A;
  assign C = A;
  assign CtlAck = AAck;
endmodule

module FourP_DRail_ADD (
  input  [1:0] A,
  input  [1:0] B,
  input  [1:0] C,
  output [1:0] S,
  output [1:0] D
);

  wire c_element_1_c, c_element_2_c, tripplec_element_1_d, tripplec_element_2_d, tripplec_element_3_d,
       tripplec_element_4_d, tripplec_element_5_d, tripplec_element_6_d, tripplec_element_7_d,
       tripplec_element_8_d;

  TrippleC_Element tripplec_element_1 (.A(A[0]), .B(B[0]), .C(C[0]), .D(tripplec_element_1_d));
  TrippleC_Element tripplec_element_2 (.A(A[0]), .B(B[0]), .C(C[1]), .D(tripplec_element_2_d));
  TrippleC_Element tripplec_element_3 (.A(A[0]), .B(B[1]), .C(C[0]), .D(tripplec_element_3_d));
  TrippleC_Element tripplec_element_4 (.A(A[0]), .B(B[1]), .C(C[1]), .D(tripplec_element_4_d));
  TrippleC_Element tripplec_element_5 (.A(A[1]), .B(B[0]), .C(C[0]), .D(tripplec_element_5_d));
  TrippleC_Element tripplec_element_6 (.A(A[1]), .B(B[0]), .C(C[0]), .D(tripplec_element_6_d));
  TrippleC_Element tripplec_element_7 (.A(A[1]), .B(B[1]), .C(C[0]), .D(tripplec_element_7_d));
  TrippleC_Element tripplec_element_8 (.A(A[1]), .B(B[1]), .C(C[1]), .D(tripplec_element_8_d));
  C_Element c_element_1 (.A(B[1]), .B(A[1]), .C(c_element_1_c));
  C_Element c_element_2 (.A(A[0]), .B(B[0]), .C(c_element_2_c));
  or or_1 (S[1], tripplec_element_2_d, tripplec_element_3_d, tripplec_element_5_d, tripplec_element_8_d);
  or or_2 (S[0], tripplec_element_1_d, tripplec_element_4_d, tripplec_element_6_d, tripplec_element_7_d);
  or or_3 (D[1], tripplec_element_4_d, tripplec_element_6_d, c_element_1_c);
  or or_4 (D[0], tripplec_element_3_d, tripplec_element_5_d, c_element_2_c);
endmodule

module FourP_BundD_Fork (
  input  A,
  input  AReq,
  input  BAck,
  input  CAck,
  output B,
  output C,
  output BReq,
  output CReq,
  output AAck
);

  C_Element c_element_1 (.A(CAck), .B(BAck), .C(AAck));

  assign B = A;
  assign BReq = AReq;
  assign C = A;
  assign CReq = AReq;
endmodule

module FourP_DRail_Fork (
  input  CAck,
  input  [1:0] A,
  input  BAck,
  output AAck,
  output [1:0] B,
  output [1:0] C
);

  C_Element c_element_1 (.A(BAck), .B(CAck), .C(AAck));

  assign B = A;
  assign C = A;
endmodule

module FourP_BundD_Join (
  input  CAck,
  input  AReq,
  input  BReq,
  input  A,
  input  B,
  output AAck,
  output BAck,
  output CReq,
  output [1:0] C
);

  C_Element c_element_1 (.A(AReq), .B(BReq), .C(CReq));

  assign AAck = CAck;
  assign BAck = CAck;
  assign C = {B, A};
endmodule

module FourP_DRail_Join (
  input  CAck,
  input  [1:0] A,
  input  [1:0] B,
  output AAck,
  output [3:0] C,
  output BAck
);


  assign AAck = CAck;
  assign BAck = CAck;
  assign C = {B, A};
endmodule

module FourP_BundD_Merge (
  input  CAck,
  input  AReq,
  input  BReq,
  input  A,
  input  B,
  output AAck,
  output CReq,
  output BAck,
  output C
);

  C_Element c_element_1 (.A(AReq), .B(CAck), .C(AAck));
  C_Element c_element_2 (.A(BReq), .B(CAck), .C(BAck));
  Multiplexer multiplexer_1 (.in0(A), .in1(B), .out(C), .sel(BReq));
  or or_1 (CReq, AReq, BReq);
endmodule

module TrippleC_Element (
  input  A,
  input  B,
  input  C,
  output D
);

  wire c_element_1_c;

  C_Element c_element_1 (.A(A), .B(B), .C(c_element_1_c));
  C_Element c_element_2 (.A(c_element_1_c), .B(C), .C(D));
endmodule
