// Logisim project AsynchronousCircuitry.circ as structural Verilog: 7 circuits, main circuit EdgeDetector
module EdgeDetector (
  input  in_1,
  output out_2
);

  wire not_1_out, not_2_out, not_3_out;

  not not_1 (not_1_out, in_1);
  not not_2 (not_2_out, not_1_out);
  not not_3 (not_3_out, not_2_out);
  xnor xnor_1 (out_2, in_1, not_3_out);
endmodule

module DRailBitReceiver (
  input  AckSignal,
  input  [1:0] Rail,
  output Changed,
  output Value
);

  wire edgedetector_1_out_2, edgedetector_2_out_2, edgedetector_3_out_2, or_1_out;

  EdgeDetector edgedetector_1 (.in_1(AckSignal), .out_2(edgedetector_1_out_2));
  EdgeDetector edgedetector_2 (.in_1(Rail[1]), .out_2(edgedetector_2_out_2));
  EdgeDetector edgedetector_3 (.in_1(Rail[0]), .out_2(edgedetector_3_out_2));
  or or_1 (or_1_out, edgedetector_3_out_2, edgedetector_2_out_2);
  S_R_Flip_Flop s_r_ff_1 (
    .Q(Value), .reset(edgedetector_3_out_2), .preset(edgedetector_2_out_2));  // open: S, R, clk, Qn
  S_R_Flip_Flop s_r_ff_2 (.Q(Changed), .reset(edgedetector_1_out_2), .preset(or_1_out));  // open: S, R, clk, Qn
endmodule

module PosEdgeDetector (
  input  in_1,
  output out_2
);

  wire not_1_out, not_2_out, not_3_out;

  not not_1 (not_1_out, in_1);
  not not_2 (not_2_out, not_1_out);
  and and_1 (out_2, in_1, not_3_out);
  not not_3 (not_3_out, not_2_out);
endmodule

module DRailByteReceiver (
  input  Stop,
  input  ReadyDelay,
  input  [15:0] DualRailByte,
  input  OtherBytesChanged,
  output DelayStart,
  output Acknowledge,
  output AllChanged,
  output [7:0] Byte
);

  wire and_1_out, and_2_out, and_3_out, and_4_out, and_5_out, and_6_out, and_7_out, and_9_out,
       drailbitreceiver_1_changed, drailbitreceiver_2_changed, drailbitreceiver_3_changed,
       drailbitreceiver_4_changed, drailbitreceiver_5_changed, drailbitreceiver_6_changed,
       drailbitreceiver_7_changed, drailbitreceiver_8_changed, edgedetector_1_out_2, not_1_out,
       posedgedetector_1_out_2, s_r_ff_1_q;
  wire [7:0] drailbitreceiver_1_value;

  DRailBitReceiver drailbitreceiver_1 (
    .AckSignal(Acknowledge), .Rail(DualRailByte[1:0]), .Changed(drailbitreceiver_1_changed),
    .Value(drailbitreceiver_1_value[0]));
  DRailBitReceiver drailbitreceiver_2 (
    .AckSignal(Acknowledge), .Rail(DualRailByte[3:2]), .Changed(drailbitreceiver_2_changed),
    .Value(drailbitreceiver_1_value[1]));
  DRailBitReceiver drailbitreceiver_3 (
    .AckSignal(Acknowledge), .Rail(DualRailByte[5:4]), .Changed(drailbitreceiver_3_changed),
    .Value(drailbitreceiver_1_value[2]));
  DRailBitReceiver drailbitreceiver_4 (
    .AckSignal(Acknowledge), .Rail(DualRailByte[7:6]), .Changed(drailbitreceiver_4_changed),
    .Value(drailbitreceiver_1_value[3]));
  DRailBitReceiver drailbitreceiver_5 (
    .AckSignal(Acknowledge), .Rail(DualRailByte[9:8]), .Changed(drailbitreceiver_5_changed),
    .Value(drailbitreceiver_1_value[4]));
  DRailBitReceiver drailbitreceiver_6 (
    .AckSignal(Acknowledge), .Rail(DualRailByte[11:10]), .Changed(drailbitreceiver_6_changed),
    .Value(drailbitreceiver_1_value[5]));
  DRailBitReceiver drailbitreceiver_7 (
    .AckSignal(Acknowledge), .Rail(DualRailByte[13:12]), .Changed(drailbitreceiver_7_changed),
    .Value(drailbitreceiver_1_value[6]));
  DRailBitReceiver drailbitreceiver_8 (
    .AckSignal(Acknowledge), .Rail(DualRailByte[15:14]), .Changed(drailbitreceiver_8_changed),
    .Value(drailbitreceiver_1_value[7]));
  and and_1 (and_1_out, drailbitreceiver_1_changed, drailbitreceiver_2_changed);
  and and_2 (and_2_out, and_1_out, and_3_out);
  and and_3 (and_3_out, drailbitreceiver_3_changed, drailbitreceiver_4_changed);
  and and_4 (and_4_out, drailbitreceiver_5_changed, drailbitreceiver_6_changed);
  and and_5 (and_5_out, and_4_out, and_6_out);
  and and_6 (and_6_out, drailbitreceiver_7_changed, drailbitreceiver_8_changed);
  Register register_1 (.D(drailbitreceiver_1_value), .en(1'b1), .clk(posedgedetector_1_out_2), .Q(Byte));  // open: clr
  and and_7 (and_7_out, and_2_out, and_5_out);
  and and_8 (AllChanged, OtherBytesChanged, and_7_out);
  PosEdgeDetector posedgedetector_1 (.in_1(AllChanged), .out_2(posedgedetector_1_out_2));
  T_Flip_Flop t_ff_1 (.T(1'b1), .clk(posedgedetector_1_out_2), .Q(DelayStart));  // open: Qn, reset, preset
  EdgeDetector edgedetector_1 (.in_1(ReadyDelay), .out_2(edgedetector_1_out_2));
  S_R_Flip_Flop s_r_ff_1 (
    .Q(s_r_ff_1_q), .reset(posedgedetector_1_out_2), .preset(edgedetector_1_out_2));  // open: S, R, clk, Qn
  not not_1 (not_1_out, Stop);
  and and_9 (and_9_out, not_1_out, s_r_ff_1_q);
  T_Flip_Flop t_ff_2 (.T(1'b1), .clk(and_9_out), .Q(Acknowledge));  // open: Qn, reset, preset

  // Other names for the same wires on the sheet: Ack = Acknowledge
endmodule

module DRailByteSender (
  input  Acknowledge,
  input  Request,
  input  [7:0] Byte,
  output Fertig,
  output [15:0] DualRailByte
);

  wire edgedetector_1_out_2, edgedetector_2_out_2, not_1_out, not_2_out, not_3_out, not_4_out, not_5_out,
       not_6_out, not_7_out, not_8_out, posedgedetector_1_out_2, s_r_ff_1_q;

  EdgeDetector edgedetector_1 (.in_1(Request), .out_2(edgedetector_1_out_2));
  S_R_Flip_Flop s_r_ff_1 (
    .Q(s_r_ff_1_q), .reset(edgedetector_2_out_2), .preset(edgedetector_1_out_2));  // open: S, R, clk, Qn
  EdgeDetector edgedetector_2 (.in_1(Acknowledge), .out_2(edgedetector_2_out_2));
  S_R_Flip_Flop Empfangen (
    .Q(Fertig), .reset(posedgedetector_1_out_2), .preset(edgedetector_2_out_2));  // open: S, R, clk, Qn
  PosEdgeDetector posedgedetector_1 (.in_1(s_r_ff_1_q), .out_2(posedgedetector_1_out_2));
  T_Flip_Flop t_ff_1 (.T(not_1_out), .clk(posedgedetector_1_out_2), .Q(DualRailByte[0]));  // open: Qn, reset, preset
  not not_1 (not_1_out, Byte[0]);
  T_Flip_Flop t_ff_2 (.T(Byte[0]), .clk(posedgedetector_1_out_2), .Q(DualRailByte[1]));  // open: Qn, reset, preset
  T_Flip_Flop t_ff_3 (.T(not_2_out), .clk(posedgedetector_1_out_2), .Q(DualRailByte[2]));  // open: Qn, reset, preset
  not not_2 (not_2_out, Byte[1]);
  T_Flip_Flop t_ff_4 (.T(Byte[1]), .clk(posedgedetector_1_out_2), .Q(DualRailByte[3]));  // open: Qn, reset, preset
  T_Flip_Flop t_ff_5 (.T(not_3_out), .clk(posedgedetector_1_out_2), .Q(DualRailByte[4]));  // open: Qn, reset, preset
  not not_3 (not_3_out, Byte[2]);
  T_Flip_Flop t_ff_6 (.T(Byte[2]), .clk(posedgedetector_1_out_2), .Q(DualRailByte[5]));  // open: Qn, reset, preset
  T_Flip_Flop t_ff_7 (.T(not_4_out), .clk(posedgedetector_1_out_2), .Q(DualRailByte[6]));  // open: Qn, reset, preset
  not not_4 (not_4_out, Byte[3]);
  T_Flip_Flop t_ff_8 (.T(Byte[3]), .clk(posedgedetector_1_out_2), .Q(DualRailByte[7]));  // open: Qn, reset, preset
  T_Flip_Flop t_ff_9 (.T(not_5_out), .clk(posedgedetector_1_out_2), .Q(DualRailByte[8]));  // open: Qn, reset, preset
  not not_5 (not_5_out, Byte[4]);
  T_Flip_Flop t_ff_10 (.T(Byte[4]), .clk(posedgedetector_1_out_2), .Q(DualRailByte[9]));  // open: Qn, reset, preset
  T_Flip_Flop t_ff_11 (.T(not_6_out), .clk(posedgedetector_1_out_2), .Q(DualRailByte[10]));  // open: Qn, reset, preset
  not not_6 (not_6_out, Byte[5]);
  T_Flip_Flop t_ff_12 (.T(Byte[5]), .clk(posedgedetector_1_out_2), .Q(DualRailByte[11]));  // open: Qn, reset, preset
  T_Flip_Flop t_ff_13 (.T(not_7_out), .clk(posedgedetector_1_out_2), .Q(DualRailByte[12]));  // open: Qn, reset, preset
  not not_7 (not_7_out, Byte[6]);
  T_Flip_Flop t_ff_14 (.T(Byte[6]), .clk(posedgedetector_1_out_2), .Q(DualRailByte[13]));  // open: Qn, reset, preset
  T_Flip_Flop t_ff_15 (.T(not_8_out), .clk(posedgedetector_1_out_2), .Q(DualRailByte[14]));  // open: Qn, reset, preset
  not not_8 (not_8_out, Byte[7]);
  T_Flip_Flop t_ff_16 (.T(Byte[7]), .clk(posedgedetector_1_out_2), .Q(DualRailByte[15]));  // open: Qn, reset, preset
endmodule

module Test (
  input  in_1,
  input  [7:0] in_2
);

  wire buffer_1_out, buffer_2_out, buffer_3_out, buffer_4_out, buffer_5_out, buffer_6_out, buffer_7_out,
       buffer_8_out, button_1_out, drailbytereceiver_1_acknowledge, drailbytereceiver_1_allchanged,
       drailbytereceiver_1_delaystart, drailbytesender_1_fertig;
  wire [15:0] drailbytesender_1_dualrailbyte;

  Button button_1 (.out(button_1_out));
  DRailByteSender drailbytesender_1 (
    .Acknowledge(drailbytereceiver_1_delaystart), .Request(button_1_out), .Byte(in_2),
    .Fertig(drailbytesender_1_fertig), .DualRailByte(drailbytesender_1_dualrailbyte));
  DRailByteReceiver drailbytereceiver_1 (
    .Stop(in_1), .ReadyDelay(buffer_8_out), .DualRailByte(drailbytesender_1_dualrailbyte),
    .DelayStart(drailbytereceiver_1_delaystart), .Acknowledge(drailbytereceiver_1_acknowledge),
    .AllChanged(drailbytereceiver_1_allchanged));  // open: OtherBytesChanged, Byte
  buf buffer_1 (buffer_1_out, drailbytereceiver_1_acknowledge);
  // Probe on drailbytereceiver_1_allchanged
  buf buffer_2 (buffer_2_out, buffer_1_out);
  buf buffer_3 (buffer_3_out, buffer_2_out);
  buf buffer_4 (buffer_4_out, buffer_3_out);
  buf buffer_5 (buffer_5_out, buffer_4_out);
  buf buffer_6 (buffer_6_out, buffer_5_out);
  buf buffer_7 (buffer_7_out, buffer_6_out);
  buf buffer_8 (buffer_8_out, buffer_7_out);
endmodule

module DRailBitReceiverFull (
  input  Stop,
  input  ReadyDelay,
  input  [1:0] DualRailBit,
  input  OtherBytesChanged,
  output DelayStart,
  output Acknowledge,
  output AllChanged,
  output Bit
);

  wire and_2_out, drailbitreceiver_1_changed, drailbitreceiver_1_value, edgedetector_1_out_2, not_1_out,
       posedgedetector_1_out_2, s_r_ff_1_q;

  DRailBitReceiver drailbitreceiver_1 (
    .AckSignal(Acknowledge), .Rail(DualRailBit), .Changed(drailbitreceiver_1_changed),
    .Value(drailbitreceiver_1_value));
  D_Flip_Flop d_ff_1 (.D(drailbitreceiver_1_value), .clk(posedgedetector_1_out_2), .Q(Bit));  // open: Qn, preset, reset
  and and_1 (AllChanged, OtherBytesChanged, drailbitreceiver_1_changed);
  PosEdgeDetector posedgedetector_1 (.in_1(AllChanged), .out_2(posedgedetector_1_out_2));
  T_Flip_Flop t_ff_1 (.T(1'b1), .clk(posedgedetector_1_out_2), .Q(DelayStart));  // open: Qn, reset, preset
  EdgeDetector edgedetector_1 (.in_1(ReadyDelay), .out_2(edgedetector_1_out_2));
  S_R_Flip_Flop s_r_ff_1 (
    .Q(s_r_ff_1_q), .reset(posedgedetector_1_out_2), .preset(edgedetector_1_out_2));  // open: S, R, clk, Qn
  not not_1 (not_1_out, Stop);
  and and_2 (and_2_out, not_1_out, s_r_ff_1_q);
  T_Flip_Flop t_ff_2 (.T(1'b1), .clk(and_2_out), .Q(Acknowledge));  // open: Qn, reset, preset

  // Other names for the same wires on the sheet: Ack = Acknowledge
endmodule
